// Logisim project cpu24_团队2.1.1.circ as structural Verilog: 9 circuits, main circuit ◆单周期硬布线控制器
// 单周期硬布线控制器
module \单周期硬布线控制器  (
  input  [5:0] OP,
  input  [5:0] Func,
  input  [4:0] T_F,
  output [3:0] ALU_OP,
  output MemToReg,
  output MemWrite,
  output ALU_SRC,
  output RegWrite,
  output SysCALL,
  output SignedExt,
  output RegDst,
  output Beq,
  output Bne,
  output JR,
  output JMP,
  output JAL,
  output SB,
  output BEGZ,
  output ERET,
  output MFC0,
  output MTC0
);

  wire nor_1_out, nor_2_out, nor_3_out, nor_4_out;

  \运算控制器自动生成  \u_运算控制器自动生成_1  (
    .OP0(OP[0]), .OP1(OP[1]), .OP2(OP[2]), .OP3(OP[3]), .OP4(OP[4]), .OP5(OP[5]), .F0(Func[0]), .F1(Func[1]),
    .F2(Func[2]), .F3(Func[3]), .F4(Func[4]), .F5(Func[5]), .S0(ALU_OP[0]), .S1(ALU_OP[1]), .S2(ALU_OP[2]),
    .S3(ALU_OP[3]));
  \控制信号自动生成  \u_控制信号自动生成_1  (
    .OP0(OP[0]), .OP1(OP[1]), .OP2(OP[2]), .OP3(OP[3]), .OP4(OP[4]), .OP5(OP[5]), .F0(Func[0]), .F1(Func[1]),
    .F2(Func[2]), .F3(Func[3]), .F4(Func[4]), .F5(Func[5]), .MemToReg(MemToReg), .MemWrite(MemWrite),
    .ALU_SRC(ALU_SRC), .RegWrite(RegWrite), .SysCALL(SysCALL), .SignedExt(SignedExt), .RegDst(RegDst),
    .BEQ(Beq), .BNE(Bne), .JR(JR), .JUMP(JMP), .JAL(JAL));
  \额外控制信号生成  \u_额外控制信号生成_1  (
    .OP0(OP[0]), .OP1(OP[1]), .OP2(OP[2]), .OP3(OP[3]), .OP4(OP[4]), .OP5(OP[5]), .SB(SB), .BEGZ(BEGZ));
  nor nor_1 (nor_1_out, OP[0], OP[1], OP[2], OP[3], ~OP[4], OP[5]);  // NOR_Gate
  nor nor_2 (nor_2_out, Func[0], Func[1], Func[2], ~Func[3], ~Func[4], Func[5]);  // NOR_Gate
  nor nor_3 (nor_3_out, T_F[0], T_F[1], T_F[2], T_F[3], T_F[4]);
  nor nor_4 (nor_4_out, T_F[0], T_F[1], ~T_F[2], T_F[3], T_F[4]);  // NOR_Gate
  and and_1 (ERET, nor_1_out, nor_2_out);
  and and_2 (MFC0, nor_1_out, nor_3_out);
  and and_3 (MTC0, nor_1_out, nor_4_out);

  // Other names for the same wires on the sheet: OP_CODE[5:0] = OP

  // Notes on the sheet:
  //   运算器控制器，根据指令生成运算器功能选择信号
  //   控制信号生成，产生数据通路需要的其他控制信号
endmodule

// 运算器控制器
module \运算控制器自动生成  (
  input  OP0,
  input  OP1,
  input  OP2,
  input  OP3,
  input  OP4,
  input  OP5,
  input  F0,
  input  F1,
  input  F2,
  input  F3,
  input  F4,
  input  F5,
  output S0,
  output S1,
  output S2,
  output S3
);

  wire and_1_out, and_2_out, and_3_out, and_4_out, and_5_out, and_6_out, and_7_out, and_8_out, and_9_out,
       and_10_out, and_11_out, and_12_out, and_13_out, and_14_out, and_15_out, and_16_out, and_17_out,
       and_18_out, and_19_out, and_20_out, and_21_out, and_22_out, and_23_out, and_24_out, and_25_out,
       and_26_out, and_27_out, and_28_out, and_29_out, and_30_out, and_31_out, and_32_out, and_33_out,
       and_34_out, and_35_out, and_36_out, and_37_out, and_38_out, not_1_out, not_2_out, not_3_out,
       not_4_out, not_5_out, not_6_out, not_7_out, not_8_out, not_9_out, not_10_out, not_11_out, not_12_out,
       not_13_out, not_14_out, not_15_out, not_16_out, not_17_out, not_18_out, not_19_out, not_20_out,
       not_21_out, not_22_out, not_23_out, not_24_out, not_25_out, not_26_out, not_27_out, not_28_out,
       not_29_out, not_30_out, not_31_out, not_32_out, not_33_out, not_34_out, not_35_out, not_36_out,
       not_37_out, not_38_out, not_39_out, not_40_out, not_41_out, not_42_out, not_43_out, not_44_out,
       not_45_out, not_46_out, not_47_out, not_48_out, not_49_out, not_50_out, not_51_out, not_52_out,
       not_53_out, not_54_out, not_55_out, not_56_out, not_57_out, not_58_out, not_59_out, not_60_out,
       not_61_out, not_62_out, not_63_out, not_64_out, not_65_out, not_66_out, not_67_out, not_68_out,
       not_69_out, not_70_out, not_71_out, not_72_out, not_73_out, not_74_out, not_75_out, not_76_out,
       not_77_out, not_78_out, not_79_out, not_80_out, not_81_out, not_82_out, not_83_out, not_84_out,
       not_85_out, not_86_out, not_87_out, not_88_out, not_89_out, not_90_out, not_91_out, not_92_out,
       not_93_out, not_94_out, not_95_out, not_96_out, not_97_out, not_98_out, not_99_out, not_100_out,
       not_101_out, not_102_out, not_103_out, not_104_out, not_105_out, not_106_out, not_107_out,
       not_108_out, not_109_out, not_110_out, not_111_out, not_112_out, not_113_out, not_114_out,
       not_115_out, not_116_out, not_117_out, not_118_out, not_119_out, not_120_out, not_121_out,
       not_122_out, not_123_out, not_124_out, not_125_out, not_126_out, not_127_out, not_128_out,
       not_129_out, not_130_out, not_131_out, not_132_out, not_133_out, not_134_out, not_135_out,
       not_136_out, not_137_out, not_138_out, not_139_out, not_140_out, not_141_out, not_142_out,
       not_143_out, not_144_out, not_145_out, not_146_out, not_147_out, not_148_out, not_149_out,
       not_150_out, not_151_out, not_152_out, not_153_out, not_154_out, not_155_out, not_156_out,
       not_157_out, not_158_out, not_159_out, not_160_out, not_161_out, not_162_out, not_163_out,
       not_164_out, not_165_out, not_166_out, not_167_out, not_168_out, not_169_out, not_170_out,
       not_171_out, not_172_out, not_173_out, not_174_out, not_175_out, not_176_out, not_177_out,
       not_178_out, not_179_out, not_180_out, not_181_out, not_182_out, not_183_out, not_184_out,
       not_185_out, not_186_out, not_187_out, not_188_out, not_189_out, not_190_out, not_191_out,
       not_192_out, not_193_out, not_194_out, not_195_out, not_196_out, not_197_out, not_198_out,
       not_199_out, not_200_out, not_201_out, not_202_out, not_203_out, not_204_out, not_205_out,
       not_206_out, not_207_out, not_208_out, not_209_out, not_210_out, not_211_out, not_212_out,
       not_213_out, not_214_out, not_215_out, not_216_out, not_217_out, not_218_out, not_219_out,
       not_220_out, not_221_out, not_222_out, not_223_out, not_224_out, not_225_out, not_226_out,
       not_227_out, not_228_out, not_229_out, not_230_out, not_231_out, not_232_out, not_233_out,
       not_234_out, not_235_out, not_236_out, not_237_out, not_238_out, not_239_out, not_240_out,
       not_241_out, not_242_out, not_243_out, not_244_out, not_245_out;

  not not_1 (not_1_out, OP1);
  not not_2 (not_2_out, OP2);
  not not_3 (not_3_out, OP4);
  not not_4 (not_4_out, OP5);
  not not_5 (not_5_out, F0);
  not not_6 (not_6_out, F1);
  not not_7 (not_7_out, F3);
  not not_8 (not_8_out, F4);
  not not_9 (not_9_out, OP1);
  not not_10 (not_10_out, OP2);
  not not_11 (not_11_out, OP4);
  not not_12 (not_12_out, OP5);
  not not_13 (not_13_out, F0);
  not not_14 (not_14_out, F3);
  not not_15 (not_15_out, F4);
  not not_16 (not_16_out, OP1);
  not not_17 (not_17_out, OP2);
  not not_18 (not_18_out, OP4);
  not not_19 (not_19_out, OP5);
  not not_20 (not_20_out, F0);
  not not_21 (not_21_out, F2);
  not not_22 (not_22_out, F4);
  not not_23 (not_23_out, OP1);
  not not_24 (not_24_out, OP2);
  not not_25 (not_25_out, OP4);
  not not_26 (not_26_out, OP5);
  not not_27 (not_27_out, F2);
  not not_28 (not_28_out, F3);
  not not_29 (not_29_out, F4);
  not not_30 (not_30_out, F5);
  not not_31 (not_31_out, OP0);
  not not_32 (not_32_out, OP1);
  not not_33 (not_33_out, OP2);
  not not_34 (not_34_out, OP4);
  not not_35 (not_35_out, OP0);
  not not_36 (not_36_out, OP1);
  not not_37 (not_37_out, OP4);
  not not_38 (not_38_out, OP5);
  not not_39 (not_39_out, OP0);
  not not_40 (not_40_out, OP2);
  not not_41 (not_41_out, OP4);
  not not_42 (not_42_out, OP5);
  not not_43 (not_43_out, OP0);
  not not_44 (not_44_out, OP1);
  not not_45 (not_45_out, OP5);
  not not_46 (not_46_out, F0);
  not not_47 (not_47_out, F2);
  not not_48 (not_48_out, F3);
  not not_49 (not_49_out, F4);
  not not_50 (not_50_out, F5);
  not not_51 (not_51_out, OP1);
  not not_52 (not_52_out, OP2);
  not not_53 (not_53_out, OP4);
  not not_54 (not_54_out, OP5);
  not not_55 (not_55_out, OP2);
  not not_56 (not_56_out, OP4);
  not not_57 (not_57_out, OP1);
  not not_58 (not_58_out, OP2);
  not not_59 (not_59_out, OP3);
  not not_60 (not_60_out, OP4);
  not not_61 (not_61_out, OP5);
  not not_62 (not_62_out, F0);
  not not_63 (not_63_out, F1);
  not not_64 (not_64_out, F3);
  not not_65 (not_65_out, F4);
  not not_66 (not_66_out, OP1);
  not not_67 (not_67_out, OP2);
  not not_68 (not_68_out, OP3);
  not not_69 (not_69_out, OP4);
  not not_70 (not_70_out, OP5);
  not not_71 (not_71_out, F0);
  not not_72 (not_72_out, F2);
  not not_73 (not_73_out, F3);
  not not_74 (not_74_out, F4);
  not not_75 (not_75_out, OP1);
  not not_76 (not_76_out, OP2);
  not not_77 (not_77_out, OP3);
  not not_78 (not_78_out, OP4);
  not not_79 (not_79_out, OP5);
  not not_80 (not_80_out, F0);
  not not_81 (not_81_out, F2);
  not not_82 (not_82_out, F4);
  not not_83 (not_83_out, OP1);
  not not_84 (not_84_out, OP2);
  not not_85 (not_85_out, OP3);
  not not_86 (not_86_out, OP4);
  not not_87 (not_87_out, OP5);
  not not_88 (not_88_out, F3);
  not not_89 (not_89_out, F4);
  not not_90 (not_90_out, OP0);
  not not_91 (not_91_out, OP1);
  not not_92 (not_92_out, OP4);
  not not_93 (not_93_out, OP5);
  not not_94 (not_94_out, OP0);
  not not_95 (not_95_out, OP1);
  not not_96 (not_96_out, OP5);
  not not_97 (not_97_out, F0);
  not not_98 (not_98_out, F2);
  not not_99 (not_99_out, F3);
  not not_100 (not_100_out, F4);
  not not_101 (not_101_out, F5);
  not not_102 (not_102_out, OP0);
  not not_103 (not_103_out, OP2);
  not not_104 (not_104_out, OP4);
  not not_105 (not_105_out, OP5);
  not not_106 (not_106_out, OP1);
  not not_107 (not_107_out, OP2);
  not not_108 (not_108_out, OP3);
  not not_109 (not_109_out, OP4);
  not not_110 (not_110_out, OP5);
  not not_111 (not_111_out, OP5);
  not not_112 (not_112_out, OP4);
  not not_113 (not_113_out, OP3);
  not not_114 (not_114_out, OP2);
  not not_115 (not_115_out, OP1);
  not not_116 (not_116_out, OP0);
  not not_117 (not_117_out, F4);
  not not_118 (not_118_out, F3);
  not not_119 (not_119_out, F2);
  not not_120 (not_120_out, F1);
  not not_121 (not_121_out, F0);
  not not_122 (not_122_out, OP5);
  not not_123 (not_123_out, OP4);
  not not_124 (not_124_out, OP3);
  not not_125 (not_125_out, OP2);
  not not_126 (not_126_out, OP1);
  not not_127 (not_127_out, OP0);
  not not_128 (not_128_out, F4);
  not not_129 (not_129_out, F3);
  not not_130 (not_130_out, F2);
  not not_131 (not_131_out, F1);
  not not_132 (not_132_out, OP5);
  not not_133 (not_133_out, OP4);
  not not_134 (not_134_out, OP3);
  not not_135 (not_135_out, OP2);
  not not_136 (not_136_out, OP1);
  not not_137 (not_137_out, OP0);
  not not_138 (not_138_out, F4);
  not not_139 (not_139_out, F3);
  not not_140 (not_140_out, F2);
  not not_141 (not_141_out, F0);
  not not_142 (not_142_out, OP5);
  not not_143 (not_143_out, OP4);
  not not_144 (not_144_out, OP3);
  not not_145 (not_145_out, OP2);
  not not_146 (not_146_out, OP1);
  not not_147 (not_147_out, OP0);
  not not_148 (not_148_out, F4);
  not not_149 (not_149_out, F3);
  not not_150 (not_150_out, F1);
  not not_151 (not_151_out, F0);
  not not_152 (not_152_out, OP5);
  not not_153 (not_153_out, OP4);
  not not_154 (not_154_out, OP3);
  not not_155 (not_155_out, OP2);
  not not_156 (not_156_out, OP1);
  not not_157 (not_157_out, OP0);
  not not_158 (not_158_out, F4);
  not not_159 (not_159_out, F2);
  not not_160 (not_160_out, OP5);
  not not_161 (not_161_out, OP4);
  not not_162 (not_162_out, OP2);
  not not_163 (not_163_out, OP1);
  not not_164 (not_164_out, OP0);
  not not_165 (not_165_out, OP5);
  not not_166 (not_166_out, OP4);
  not not_167 (not_167_out, OP1);
  not not_168 (not_168_out, OP0);
  not not_169 (not_169_out, OP5);
  not not_170 (not_170_out, OP4);
  not not_171 (not_171_out, OP2);
  not not_172 (not_172_out, OP1);
  not not_173 (not_173_out, OP4);
  not not_174 (not_174_out, OP3);
  not not_175 (not_175_out, OP2);
  not not_176 (not_176_out, OP4);
  not not_177 (not_177_out, OP2);
  not not_178 (not_178_out, OP5);
  not not_179 (not_179_out, OP4);
  not not_180 (not_180_out, OP3);
  not not_181 (not_181_out, OP2);
  not not_182 (not_182_out, OP1);
  not not_183 (not_183_out, OP0);
  not not_184 (not_184_out, F4);
  not not_185 (not_185_out, F3);
  not not_186 (not_186_out, F2);
  not not_187 (not_187_out, OP4);
  not not_188 (not_188_out, OP2);
  not not_189 (not_189_out, OP1);
  not not_190 (not_190_out, OP0);
  not not_191 (not_191_out, OP5);
  not not_192 (not_192_out, OP4);
  not not_193 (not_193_out, OP3);
  not not_194 (not_194_out, OP2);
  not not_195 (not_195_out, OP1);
  not not_196 (not_196_out, OP0);
  not not_197 (not_197_out, F4);
  not not_198 (not_198_out, F3);
  not not_199 (not_199_out, F1);
  not not_200 (not_200_out, OP5);
  not not_201 (not_201_out, OP4);
  not not_202 (not_202_out, OP3);
  not not_203 (not_203_out, OP2);
  not not_204 (not_204_out, OP1);
  not not_205 (not_205_out, OP0);
  not not_206 (not_206_out, F4);
  not not_207 (not_207_out, F3);
  not not_208 (not_208_out, OP5);
  not not_209 (not_209_out, OP4);
  not not_210 (not_210_out, OP3);
  not not_211 (not_211_out, OP2);
  not not_212 (not_212_out, OP1);
  not not_213 (not_213_out, OP0);
  not not_214 (not_214_out, F4);
  not not_215 (not_215_out, F2);
  not not_216 (not_216_out, F0);
  not not_217 (not_217_out, OP5);
  not not_218 (not_218_out, OP4);
  not not_219 (not_219_out, OP3);
  not not_220 (not_220_out, OP2);
  not not_221 (not_221_out, OP1);
  not not_222 (not_222_out, OP0);
  not not_223 (not_223_out, F4);
  not not_224 (not_224_out, F2);
  not not_225 (not_225_out, OP5);
  not not_226 (not_226_out, OP4);
  not not_227 (not_227_out, OP2);
  not not_228 (not_228_out, OP0);
  not not_229 (not_229_out, OP5);
  not not_230 (not_230_out, OP4);
  not not_231 (not_231_out, OP1);
  not not_232 (not_232_out, OP5);
  not not_233 (not_233_out, OP4);
  not not_234 (not_234_out, OP3);
  not not_235 (not_235_out, OP2);
  not not_236 (not_236_out, OP1);
  not not_237 (not_237_out, OP0);
  not not_238 (not_238_out, F4);
  not not_239 (not_239_out, F3);
  not not_240 (not_240_out, F0);
  not not_241 (not_241_out, OP5);
  not not_242 (not_242_out, OP4);
  not not_243 (not_243_out, OP3);
  not not_244 (not_244_out, OP2);
  not not_245 (not_245_out, OP1);
  and and_1 (and_1_out, not_1_out, not_2_out, not_3_out, not_4_out, not_5_out, not_6_out, not_7_out, not_8_out, F5);
  and and_2 (and_2_out, not_9_out, not_10_out, not_11_out, not_12_out, not_13_out, F2, not_14_out, not_15_out, F5);
  and and_3 (and_3_out, not_16_out, not_17_out, not_18_out, not_19_out, not_20_out, F1, not_21_out, F3, not_22_out, F5);
  and and_4 (and_4_out, not_23_out, not_24_out, not_25_out, not_26_out, F0, F1, not_27_out, not_28_out, not_29_out, not_30_out);
  and and_5 (and_5_out, not_31_out, not_32_out, not_33_out, OP3, not_34_out);
  and and_6 (and_6_out, not_35_out, not_36_out, OP3, not_37_out, not_38_out);
  and and_7 (and_7_out, not_39_out, not_40_out, OP3, not_41_out, not_42_out);
  and and_8 (and_8_out, not_43_out, not_44_out, OP2, OP3, not_45_out, not_46_out, F1, not_47_out, not_48_out, not_49_out, not_50_out);
  and and_9 (and_9_out, OP0, not_51_out, not_52_out, not_53_out, not_54_out);
  and and_10 (and_10_out, OP0, OP1, not_55_out, not_56_out, OP5);
  and and_11 (and_11_out, not_57_out, not_58_out, not_59_out, not_60_out, not_61_out, not_62_out, not_63_out, F2, not_64_out, not_65_out, F5);
  and and_12 (and_12_out, not_66_out, not_67_out, not_68_out, not_69_out, not_70_out, not_71_out, F1, not_72_out, not_73_out, not_74_out);
  and and_13 (and_13_out, not_75_out, not_76_out, not_77_out, not_78_out, not_79_out, not_80_out, F1, not_81_out, not_82_out, F5);
  and and_14 (and_14_out, not_83_out, not_84_out, not_85_out, not_86_out, not_87_out, F0, F1, not_88_out, not_89_out, F5);
  and and_15 (and_15_out, not_90_out, not_91_out, OP2, OP3, not_92_out, not_93_out);
  and and_16 (and_16_out, not_94_out, not_95_out, OP2, OP3, not_96_out, not_97_out, F1, not_98_out, not_99_out, not_100_out, not_101_out);
  and and_17 (and_17_out, not_102_out, OP1, not_103_out, OP3, not_104_out, not_105_out);
  and and_18 (and_18_out, OP0, not_106_out, not_107_out, not_108_out, not_109_out, not_110_out);
  and and_19 (and_19_out, not_111_out, not_112_out, not_113_out, not_114_out, not_115_out, not_116_out, F5, not_117_out, not_118_out, not_119_out, not_120_out, not_121_out);
  and and_20 (and_20_out, not_122_out, not_123_out, not_124_out, not_125_out, not_126_out, not_127_out, F5, not_128_out, not_129_out, not_130_out, not_131_out, F0);
  and and_21 (and_21_out, not_132_out, not_133_out, not_134_out, not_135_out, not_136_out, not_137_out, F5, not_138_out, not_139_out, not_140_out, F1, not_141_out);
  and and_22 (and_22_out, not_142_out, not_143_out, not_144_out, not_145_out, not_146_out, not_147_out, F5, not_148_out, not_149_out, F2, not_150_out, not_151_out);
  and and_23 (and_23_out, not_152_out, not_153_out, not_154_out, not_155_out, not_156_out, not_157_out, F5, not_158_out, F3, not_159_out, F1, F0);
  and and_24 (and_24_out, not_160_out, not_161_out, OP3, not_162_out, not_163_out, not_164_out);
  and and_25 (and_25_out, not_165_out, not_166_out, OP3, OP2, not_167_out, not_168_out);
  and and_26 (and_26_out, not_169_out, not_170_out, OP3, not_171_out, not_172_out, OP0);
  and and_27 (and_27_out, OP5, not_173_out, not_174_out, not_175_out, OP1, OP0);
  and and_28 (and_28_out, OP5, not_176_out, OP3, not_177_out, OP1, OP0);
  and and_29 (and_29_out, not_178_out, not_179_out, not_180_out, not_181_out, not_182_out, not_183_out, F5, not_184_out, not_185_out, not_186_out, F1, F0);
  and and_30 (and_30_out, OP5, not_187_out, OP3, not_188_out, not_189_out, not_190_out);
  and and_31 (and_31_out, not_191_out, not_192_out, not_193_out, not_194_out, not_195_out, not_196_out, F5, not_197_out, not_198_out, F2, not_199_out, F0);
  and and_32 (and_32_out, not_200_out, not_201_out, not_202_out, not_203_out, not_204_out, not_205_out, F5, not_206_out, not_207_out, F2, F1, F0);
  and and_33 (and_33_out, not_208_out, not_209_out, not_210_out, not_211_out, not_212_out, not_213_out, F5, not_214_out, F3, not_215_out, F1, not_216_out);
  and and_34 (and_34_out, not_217_out, not_218_out, not_219_out, not_220_out, not_221_out, not_222_out, F5, not_223_out, F3, not_224_out, F1, F0);
  and and_35 (and_35_out, not_225_out, not_226_out, OP3, not_227_out, OP1, not_228_out);
  and and_36 (and_36_out, not_229_out, not_230_out, OP3, OP2, not_231_out, OP0);
  and and_37 (and_37_out, not_232_out, not_233_out, not_234_out, not_235_out, not_236_out, not_237_out, F5, not_238_out, not_239_out, F2, F1, not_240_out);
  and and_38 (and_38_out, not_241_out, not_242_out, not_243_out, not_244_out, not_245_out, OP0);
  or or_1 (S0, and_1_out, and_2_out, and_3_out, and_4_out, and_5_out, and_6_out, and_7_out, and_8_out, and_9_out, and_10_out);
  or or_2 (S1, and_11_out, and_12_out, and_13_out, and_14_out, and_15_out, and_16_out, and_17_out, and_18_out);
  or or_3 (S3, and_31_out, and_32_out, and_33_out, and_34_out, and_35_out, and_36_out, and_37_out, and_38_out);
  or or_4 (S2, and_19_out, and_20_out, and_21_out, and_22_out, and_23_out, and_24_out, and_25_out, and_26_out, and_27_out, and_28_out, and_29_out, and_30_out);
endmodule

// 控制信号生成
module \控制信号自动生成  (
  input  OP0,
  input  OP1,
  input  OP2,
  input  OP3,
  input  OP4,
  input  OP5,
  input  F0,
  input  F1,
  input  F2,
  input  F3,
  input  F4,
  input  F5,
  output MemToReg,
  output MemWrite,
  output ALU_SRC,
  output RegWrite,
  output SysCALL,
  output SignedExt,
  output RegDst,
  output BEQ,
  output BNE,
  output JR,
  output JUMP,
  output JAL
);

  wire and_2_out, and_3_out, and_4_out, and_5_out, and_6_out, and_7_out, and_8_out, and_9_out, and_10_out,
       and_11_out, and_12_out, and_13_out, and_14_out, and_15_out, and_16_out, and_17_out, and_18_out,
       and_19_out, and_21_out, and_22_out, and_23_out, and_24_out, and_25_out, and_26_out, and_27_out,
       and_28_out, and_29_out, and_30_out, and_31_out, not_1_out, not_2_out, not_3_out, not_4_out, not_5_out,
       not_6_out, not_7_out, not_8_out, not_9_out, not_10_out, not_11_out, not_12_out, not_13_out,
       not_14_out, not_15_out, not_16_out, not_17_out, not_18_out, not_19_out, not_20_out, not_21_out,
       not_22_out, not_23_out, not_24_out, not_25_out, not_26_out, not_27_out, not_28_out, not_29_out,
       not_30_out, not_31_out, not_32_out, not_33_out, not_34_out, not_35_out, not_36_out, not_37_out,
       not_38_out, not_39_out, not_40_out, not_41_out, not_42_out, not_43_out, not_44_out, not_45_out,
       not_46_out, not_47_out, not_48_out, not_49_out, not_50_out, not_51_out, not_52_out, not_53_out,
       not_54_out, not_55_out, not_56_out, not_57_out, not_58_out, not_59_out, not_60_out, not_61_out,
       not_62_out, not_63_out, not_64_out, not_65_out, not_66_out, not_67_out, not_68_out, not_69_out,
       not_70_out, not_71_out, not_72_out, not_73_out, not_74_out, not_75_out, not_76_out, not_77_out,
       not_78_out, not_79_out, not_80_out, not_81_out, not_82_out, not_83_out, not_84_out, not_85_out,
       not_86_out, not_87_out, not_88_out, not_89_out, not_90_out, not_91_out, not_92_out, not_93_out,
       not_94_out, not_95_out, not_96_out, not_97_out, not_98_out, not_99_out, not_100_out, not_101_out,
       not_102_out, not_103_out, not_104_out, not_105_out, not_106_out, not_107_out, not_108_out,
       not_109_out, not_110_out, not_111_out, not_112_out, not_113_out, not_114_out, not_115_out,
       not_116_out, not_117_out, not_118_out, not_119_out, not_120_out, not_121_out, not_122_out,
       not_123_out, not_124_out, not_125_out, not_126_out, not_127_out, not_128_out, not_129_out,
       not_130_out, not_131_out, not_132_out, not_133_out, not_134_out, not_135_out, not_136_out,
       not_137_out, not_138_out, not_139_out, not_140_out, not_141_out, not_142_out, not_143_out,
       not_144_out, not_145_out, not_146_out, not_147_out, not_148_out, not_149_out, not_150_out,
       not_151_out, not_152_out, not_153_out, not_154_out, not_155_out, not_156_out, not_157_out,
       not_158_out, not_159_out, not_160_out, not_161_out, not_162_out, not_163_out, not_164_out,
       not_165_out, not_166_out, not_167_out, not_168_out, not_169_out, not_170_out, not_171_out,
       not_172_out, not_173_out, not_174_out, not_175_out, not_176_out, not_177_out, not_178_out,
       not_179_out, not_180_out, not_181_out, not_182_out, not_183_out, not_184_out, not_185_out,
       not_186_out, not_187_out, not_188_out, not_189_out, not_190_out, not_191_out;

  not not_1 (not_1_out, OP4);
  not not_2 (not_2_out, OP3);
  not not_3 (not_3_out, OP2);
  not not_4 (not_4_out, OP4);
  not not_5 (not_5_out, OP2);
  not not_6 (not_6_out, OP4);
  not not_7 (not_7_out, OP2);
  not not_8 (not_8_out, OP1);
  not not_9 (not_9_out, OP0);
  not not_10 (not_10_out, OP5);
  not not_11 (not_11_out, OP4);
  not not_12 (not_12_out, OP2);
  not not_13 (not_13_out, OP1);
  not not_14 (not_14_out, OP0);
  not not_15 (not_15_out, OP5);
  not not_16 (not_16_out, OP4);
  not not_17 (not_17_out, OP1);
  not not_18 (not_18_out, OP0);
  not not_19 (not_19_out, OP5);
  not not_20 (not_20_out, OP4);
  not not_21 (not_21_out, OP2);
  not not_22 (not_22_out, OP1);
  not not_23 (not_23_out, OP5);
  not not_24 (not_24_out, OP4);
  not not_25 (not_25_out, OP2);
  not not_26 (not_26_out, OP0);
  not not_27 (not_27_out, OP5);
  not not_28 (not_28_out, OP4);
  not not_29 (not_29_out, OP1);
  not not_30 (not_30_out, OP4);
  not not_31 (not_31_out, OP3);
  not not_32 (not_32_out, OP2);
  not not_33 (not_33_out, OP4);
  not not_34 (not_34_out, OP2);
  not not_35 (not_35_out, OP4);
  not not_36 (not_36_out, OP2);
  not not_37 (not_37_out, OP1);
  not not_38 (not_38_out, OP0);
  not not_39 (not_39_out, OP0);
  not not_40 (not_40_out, OP1);
  not not_41 (not_41_out, OP2);
  not not_42 (not_42_out, OP4);
  not not_43 (not_43_out, OP5);
  not not_44 (not_44_out, F0);
  not not_45 (not_45_out, F2);
  not not_46 (not_46_out, F3);
  not not_47 (not_47_out, F4);
  not not_48 (not_48_out, OP0);
  not not_49 (not_49_out, OP1);
  not not_50 (not_50_out, OP2);
  not not_51 (not_51_out, OP4);
  not not_52 (not_52_out, OP5);
  not not_53 (not_53_out, F3);
  not not_54 (not_54_out, F4);
  not not_55 (not_55_out, OP0);
  not not_56 (not_56_out, OP1);
  not not_57 (not_57_out, OP2);
  not not_58 (not_58_out, OP4);
  not not_59 (not_59_out, OP5);
  not not_60 (not_60_out, F2);
  not not_61 (not_61_out, F3);
  not not_62 (not_62_out, F4);
  not not_63 (not_63_out, OP0);
  not not_64 (not_64_out, OP1);
  not not_65 (not_65_out, OP2);
  not not_66 (not_66_out, OP4);
  not not_67 (not_67_out, OP5);
  not not_68 (not_68_out, F2);
  not not_69 (not_69_out, F4);
  not not_70 (not_70_out, OP0);
  not not_71 (not_71_out, OP2);
  not not_72 (not_72_out, OP4);
  not not_73 (not_73_out, OP5);
  not not_74 (not_74_out, OP1);
  not not_75 (not_75_out, OP4);
  not not_76 (not_76_out, OP5);
  not not_77 (not_77_out, OP0);
  not not_78 (not_78_out, OP1);
  not not_79 (not_79_out, OP5);
  not not_80 (not_80_out, F0);
  not not_81 (not_81_out, F2);
  not not_82 (not_82_out, F3);
  not not_83 (not_83_out, F4);
  not not_84 (not_84_out, F5);
  not not_85 (not_85_out, OP2);
  not not_86 (not_86_out, OP3);
  not not_87 (not_87_out, OP4);
  not not_88 (not_88_out, OP5);
  not not_89 (not_89_out, OP4);
  not not_90 (not_90_out, OP3);
  not not_91 (not_91_out, OP2);
  not not_92 (not_92_out, OP1);
  not not_93 (not_93_out, OP0);
  not not_94 (not_94_out, F5);
  not not_95 (not_95_out, F4);
  not not_96 (not_96_out, F1);
  not not_97 (not_97_out, F0);
  not not_98 (not_98_out, OP5);
  not not_99 (not_99_out, OP4);
  not not_100 (not_100_out, OP2);
  not not_101 (not_101_out, OP1);
  not not_102 (not_102_out, OP0);
  not not_103 (not_103_out, OP5);
  not not_104 (not_104_out, OP4);
  not not_105 (not_105_out, OP2);
  not not_106 (not_106_out, OP1);
  not not_107 (not_107_out, OP5);
  not not_108 (not_108_out, OP4);
  not not_109 (not_109_out, OP2);
  not not_110 (not_110_out, OP0);
  not not_111 (not_111_out, OP4);
  not not_112 (not_112_out, OP3);
  not not_113 (not_113_out, OP2);
  not not_114 (not_114_out, OP4);
  not not_115 (not_115_out, OP2);
  not not_116 (not_116_out, OP4);
  not not_117 (not_117_out, OP2);
  not not_118 (not_118_out, OP1);
  not not_119 (not_119_out, OP0);
  not not_120 (not_120_out, OP0);
  not not_121 (not_121_out, OP1);
  not not_122 (not_122_out, OP2);
  not not_123 (not_123_out, OP3);
  not not_124 (not_124_out, OP4);
  not not_125 (not_125_out, OP5);
  not not_126 (not_126_out, F0);
  not not_127 (not_127_out, F2);
  not not_128 (not_128_out, F3);
  not not_129 (not_129_out, F4);
  not not_130 (not_130_out, OP0);
  not not_131 (not_131_out, OP1);
  not not_132 (not_132_out, OP2);
  not not_133 (not_133_out, OP3);
  not not_134 (not_134_out, OP4);
  not not_135 (not_135_out, OP5);
  not not_136 (not_136_out, F3);
  not not_137 (not_137_out, F4);
  not not_138 (not_138_out, OP0);
  not not_139 (not_139_out, OP1);
  not not_140 (not_140_out, OP2);
  not not_141 (not_141_out, OP3);
  not not_142 (not_142_out, OP4);
  not not_143 (not_143_out, OP5);
  not not_144 (not_144_out, F2);
  not not_145 (not_145_out, F3);
  not not_146 (not_146_out, F4);
  not not_147 (not_147_out, OP0);
  not not_148 (not_148_out, OP1);
  not not_149 (not_149_out, OP2);
  not not_150 (not_150_out, OP3);
  not not_151 (not_151_out, OP4);
  not not_152 (not_152_out, OP5);
  not not_153 (not_153_out, F2);
  not not_154 (not_154_out, F4);
  not not_155 (not_155_out, OP0);
  not not_156 (not_156_out, OP1);
  not not_157 (not_157_out, OP5);
  not not_158 (not_158_out, F0);
  not not_159 (not_159_out, F2);
  not not_160 (not_160_out, F3);
  not not_161 (not_161_out, F4);
  not not_162 (not_162_out, F5);
  not not_163 (not_163_out, OP5);
  not not_164 (not_164_out, OP4);
  not not_165 (not_165_out, OP3);
  not not_166 (not_166_out, OP1);
  not not_167 (not_167_out, OP0);
  not not_168 (not_168_out, OP5);
  not not_169 (not_169_out, OP4);
  not not_170 (not_170_out, OP3);
  not not_171 (not_171_out, OP1);
  not not_172 (not_172_out, OP5);
  not not_173 (not_173_out, OP4);
  not not_174 (not_174_out, OP3);
  not not_175 (not_175_out, OP2);
  not not_176 (not_176_out, OP1);
  not not_177 (not_177_out, OP0);
  not not_178 (not_178_out, F5);
  not not_179 (not_179_out, F4);
  not not_180 (not_180_out, F2);
  not not_181 (not_181_out, F1);
  not not_182 (not_182_out, F0);
  not not_183 (not_183_out, OP5);
  not not_184 (not_184_out, OP4);
  not not_185 (not_185_out, OP3);
  not not_186 (not_186_out, OP2);
  not not_187 (not_187_out, OP0);
  not not_188 (not_188_out, OP5);
  not not_189 (not_189_out, OP4);
  not not_190 (not_190_out, OP3);
  not not_191 (not_191_out, OP2);
  and and_1 (MemToReg, OP5, not_1_out, not_2_out, not_3_out, OP1, OP0);
  and and_2 (and_2_out, OP5, not_4_out, OP3, not_5_out, OP1, OP0);
  and and_3 (and_3_out, OP5, not_6_out, OP3, not_7_out, not_8_out, not_9_out);
  and and_4 (and_4_out, not_10_out, not_11_out, OP3, not_12_out, not_13_out, not_14_out);
  and and_5 (and_5_out, not_15_out, not_16_out, OP3, OP2, not_17_out, not_18_out);
  and and_6 (and_6_out, not_19_out, not_20_out, OP3, not_21_out, not_22_out, OP0);
  and and_7 (and_7_out, not_23_out, not_24_out, OP3, not_25_out, OP1, not_26_out);
  and and_8 (and_8_out, not_27_out, not_28_out, OP3, OP2, not_29_out, OP0);
  and and_9 (and_9_out, OP5, not_30_out, not_31_out, not_32_out, OP1, OP0);
  and and_10 (and_10_out, OP5, not_33_out, OP3, not_34_out, OP1, OP0);
  and and_11 (and_11_out, OP5, not_35_out, OP3, not_36_out, not_37_out, not_38_out);
  and and_12 (and_12_out, not_39_out, not_40_out, not_41_out, not_42_out, not_43_out, not_44_out, not_45_out, not_46_out, not_47_out);
  and and_13 (and_13_out, not_48_out, not_49_out, not_50_out, not_51_out, not_52_out, not_53_out, not_54_out, F5);
  and and_14 (and_14_out, not_55_out, not_56_out, not_57_out, not_58_out, not_59_out, F1, not_60_out, not_61_out, not_62_out);
  and and_15 (and_15_out, not_63_out, not_64_out, not_65_out, not_66_out, not_67_out, F1, not_68_out, not_69_out, F5);
  and and_16 (and_16_out, not_70_out, not_71_out, OP3, not_72_out, not_73_out);
  and and_17 (and_17_out, not_74_out, OP3, not_75_out, not_76_out);
  and and_18 (and_18_out, not_77_out, not_78_out, OP2, OP3, not_79_out, not_80_out, F1, not_81_out, not_82_out, not_83_out, not_84_out);
  and and_19 (and_19_out, OP0, OP1, not_85_out, not_86_out, not_87_out);
  and and_20 (SysCALL, not_88_out, not_89_out, not_90_out, not_91_out, not_92_out, not_93_out, not_94_out, not_95_out, F3, F2, not_96_out, not_97_out);
  and and_21 (and_21_out, not_98_out, not_99_out, OP3, not_100_out, not_101_out, not_102_out);
  and and_22 (and_22_out, not_103_out, not_104_out, OP3, not_105_out, not_106_out, OP0);
  and and_23 (and_23_out, not_107_out, not_108_out, OP3, not_109_out, OP1, not_110_out);
  and and_24 (and_24_out, OP5, not_111_out, not_112_out, not_113_out, OP1, OP0);
  and and_25 (and_25_out, OP5, not_114_out, OP3, not_115_out, OP1, OP0);
  and and_26 (and_26_out, OP5, not_116_out, OP3, not_117_out, not_118_out, not_119_out);
  and and_27 (and_27_out, not_120_out, not_121_out, not_122_out, not_123_out, not_124_out, not_125_out, not_126_out, not_127_out, not_128_out, not_129_out);
  and and_28 (and_28_out, not_130_out, not_131_out, not_132_out, not_133_out, not_134_out, not_135_out, not_136_out, not_137_out, F5);
  and and_29 (and_29_out, not_138_out, not_139_out, not_140_out, not_141_out, not_142_out, not_143_out, F1, not_144_out, not_145_out, not_146_out);
  and and_30 (and_30_out, not_147_out, not_148_out, not_149_out, not_150_out, not_151_out, not_152_out, F1, not_153_out, not_154_out, F5);
  and and_31 (and_31_out, not_155_out, not_156_out, OP2, OP3, OP4, not_157_out, not_158_out, F1, not_159_out, not_160_out, not_161_out, not_162_out);
  and and_32 (BEQ, not_163_out, not_164_out, not_165_out, OP2, not_166_out, not_167_out);
  and and_33 (BNE, not_168_out, not_169_out, not_170_out, OP2, not_171_out, OP0);
  and and_34 (JR, not_172_out, not_173_out, not_174_out, not_175_out, not_176_out, not_177_out, not_178_out, not_179_out, F3, not_180_out, not_181_out, not_182_out);
  and and_35 (JUMP, not_183_out, not_184_out, not_185_out, not_186_out, OP1, not_187_out);
  and and_36 (JAL, not_188_out, not_189_out, not_190_out, not_191_out, OP1, OP0);
  or or_1 (MemWrite, and_2_out, and_3_out);
  or or_2 (ALU_SRC, and_4_out, and_5_out, and_6_out, and_7_out, and_8_out, and_9_out, and_10_out, and_11_out);
  or or_3 (RegWrite, and_12_out, and_13_out, and_14_out, and_15_out, and_16_out, and_17_out, and_18_out, and_19_out);
  or or_4 (SignedExt, and_21_out, and_22_out, and_23_out, and_24_out, and_25_out, and_26_out);
  or or_5 (RegDst, and_27_out, and_28_out, and_29_out, and_30_out, and_31_out);
endmodule

// ALU
module MIPS_ALU (
  input  [4:0] shamt,
  input  [31:0] X,
  input  [31:0] Y,
  input  [3:0] AluOP,
  output Equal,
  output [31:0] Result,
  output [31:0] Result_2
);

  wire [0:0] comparator_1_lt, comparator_2_lt;
  wire [31:0] adder_1_out, AND_out, divider_1_out, divider_1_rem, multiplier_1_cout, multiplier_1_out,
       NOR_out, OR_out, shifter_1_out, shifter_2_out, shifter_3_out, subtractor_1_out, XOR_out;

  assign AND_out = X & Y;  // AND_Gate AND, 32 bits wide
  assign OR_out = X | Y;  // OR_Gate OR, 32 bits wide
  Shifter #(.width(32), .shift("ll")) shifter_1 (.in(Y), .\dist (shamt), .out(shifter_1_out));
  Shifter #(.width(32), .shift("ar")) shifter_2 (.in(Y), .\dist (shamt), .out(shifter_2_out));
  Shifter #(.width(32), .shift("lr")) shifter_3 (.in(Y), .\dist (shamt), .out(shifter_3_out));
  Multiplier #(.width(32)) multiplier_1 (.a(X), .b(Y), .out(multiplier_1_out), .cout(multiplier_1_cout));  // open: cin
  Divider #(.width(32)) divider_1 (.a(X), .b(Y), .out(divider_1_out), .rem(divider_1_rem));  // open: upper
  Adder #(.width(32)) adder_1 (.a(X), .b(Y), .out(adder_1_out));  // open: cin, cout
  Subtractor #(.width(32)) subtractor_1 (.a(X), .b(Y), .out(subtractor_1_out));  // open: bin, bout
  assign XOR_out = X ^ Y;  // XOR_Gate XOR, 32 bits wide
  assign NOR_out = ~(X | Y);  // NOR_Gate NOR, 32 bits wide
  Comparator #(.width(32), .mode("twosComplement")) comparator_1 (
    .a(X), .b(Y), .eq(Equal), .lt(comparator_1_lt[0]));  // open: gt
  Comparator #(.width(32), .mode("unsigned")) comparator_2 (.a(X), .b(Y), .lt(comparator_2_lt[0]));  // open: gt, eq
  Multiplexer #(.select(4), .width(32), .disabled("Z"), .enable("false")) multiplexer_1 (
    .in0(shifter_1_out), .in1(shifter_2_out), .in2(shifter_3_out), .in3(multiplier_1_out),
    .in4(divider_1_out), .in5(adder_1_out), .in6(subtractor_1_out), .in7(AND_out), .in8(OR_out),
    .in9(XOR_out), .in10(NOR_out), .in11({{31{1'b0}}, comparator_1_lt[0]}),
    .in12({{31{1'b0}}, comparator_2_lt[0]}), .in13({32{1'b0}}), .in14({32{1'b0}}), .in15({32{1'b0}}),
    .out(Result), .sel(AluOP));
  Multiplexer #(.select(4), .width(32), .disabled("Z"), .enable("false")) multiplexer_2 (
    .in0({32{1'b0}}), .in1({32{1'b0}}), .in2({32{1'b0}}), .in3(multiplier_1_cout), .in4(divider_1_rem),
    .in5({32{1'b0}}), .in6({32{1'b0}}), .in7({32{1'b0}}), .in8({32{1'b0}}), .in9({32{1'b0}}),
    .in10({32{1'b0}}), .in11({32{1'b0}}), .in12({32{1'b0}}), .in13({32{1'b0}}), .in14({32{1'b0}}),
    .in15({32{1'b0}}), .out(Result_2), .sel(AluOP));

  // Other names for the same wires on the sheet: Result2[31:0] = Result_2; S[3:0] = AluOP

  // Notes on the sheet:
  //   不要改变此引脚区域内容，也不要改变ALU封装形式
  //   输入引脚
  //   输出引脚
endmodule

module MIPS_Regifile (
  input  [31:0] Din,
  input  Clk,
  input  WE,
  input  [4:0] R1_num,
  input  [4:0] W_num,
  input  [4:0] R2_num,
  output [31:0] R1,
  output [31:0] R2
);

  // RegisterFile registerfile_1: pin names not known; wires that end beside it: Din, Clk, WE, W_num, R1_num, R2_num, R1, R2
endmodule

module \中断按键参考电路  (
  input  \同步清零信号 ,
  output \与中断屏蔽位与 
);

  wire \_1号中断_out , and_1_out, clock_1_out, d_ff_1_q, or_1_out, or_2_out;

  Clock #(.highDuration(1), .lowDuration(1)) clock_1 (.out(clock_1_out));
  Button \_1号中断  (.out(\_1号中断_out ));
  LED #(.active("true")) \_1号中断等待指示灯  (.in(or_1_out));
  or or_1 (or_1_out, \与中断屏蔽位与 , d_ff_1_q);
  D_Flip_Flop #(.trigger("rising"), .Pre_Clr_Positions("LEGACY"), .NegatePresetClear("false"), .enable("true"), .NewFFLayout("false")) d_ff_1 (
    .clk(\_1号中断_out ), .D(1'b1), .Q(d_ff_1_q), .reset(\与中断屏蔽位与 ));  // open: Qn, preset, en
  or or_2 (or_2_out, d_ff_1_q, \与中断屏蔽位与 );
  and and_1 (and_1_out, or_2_out, ~\同步清零信号 );  // AND_Gate
  D_Flip_Flop #(.trigger("rising"), .Pre_Clr_Positions("LEGACY"), .NegatePresetClear("false"), .enable("true"), .NewFFLayout("false")) IR1 (
    .clk(clock_1_out), .D(and_1_out), .Q(\与中断屏蔽位与 ));  // open: Qn, preset, en, reset

  // Notes on the sheet:
  //   中断信号采样参考电路
  //   Reset 
endmodule

// 额外信号
module \额外控制信号生成  (
  input  OP0,
  input  OP1,
  input  OP2,
  input  OP3,
  input  OP4,
  input  OP5,
  output SB,
  output BEGZ
);

  wire not_1_out, not_2_out, not_3_out, not_4_out, not_5_out, not_6_out, not_7_out, not_8_out, not_9_out;

  not not_1 (not_1_out, OP4);
  not not_2 (not_2_out, OP2);
  not not_3 (not_3_out, OP1);
  not not_4 (not_4_out, OP0);
  not not_5 (not_5_out, OP5);
  not not_6 (not_6_out, OP4);
  not not_7 (not_7_out, OP3);
  not not_8 (not_8_out, OP2);
  not not_9 (not_9_out, OP1);
  and and_1 (SB, OP5, not_1_out, OP3, not_2_out, not_3_out, not_4_out);
  and and_2 (BEGZ, not_5_out, not_6_out, not_7_out, not_8_out, not_9_out, OP0);
endmodule

module \输出驱动  (
  input  \同步清零_高电平有效 ,
  input  [31:0] \列数据 ,
  input  in_3,
  input  [4:0] \列选 ,
  input  \使能_低电平有效 ,
  input  \清零_高电平有效 ,
  output [31:0] _1,
  output [31:0] out_8,
  output [31:0] out_9,
  output [31:0] out_10,
  output [31:0] out_11,
  output [31:0] out_12,
  output [31:0] out_13,
  output [31:0] out_14,
  output [31:0] out_15,
  output [31:0] out_16,
  output [31:0] out_17,
  output [31:0] out_18,
  output [31:0] out_19,
  output [31:0] out_20,
  output [31:0] out_21,
  output [31:0] out_22,
  output [31:0] out_23,
  output [31:0] out_24,
  output [31:0] out_25,
  output [31:0] out_26,
  output [31:0] out_27,
  output [31:0] out_28,
  output [31:0] out_29,
  output [31:0] out_30,
  output [31:0] out_31,
  output [31:0] out_32,
  output [31:0] out_33,
  output [31:0] out_34,
  output [31:0] out_35,
  output [31:0] out_36,
  output [31:0] out_37
);

  wire decoder_1_out0, decoder_1_out1, decoder_1_out2, decoder_1_out3, decoder_1_out4, decoder_1_out5,
       decoder_1_out6, decoder_1_out7, decoder_1_out8, decoder_1_out9, decoder_1_out10, decoder_1_out11,
       decoder_1_out12, decoder_1_out13, decoder_1_out14, decoder_1_out15, decoder_1_out16, decoder_1_out17,
       decoder_1_out18, decoder_1_out19, decoder_1_out20, decoder_1_out21, decoder_1_out22, decoder_1_out23,
       decoder_1_out24, decoder_1_out25, decoder_1_out26, decoder_1_out27, decoder_1_out28, decoder_1_out29,
       decoder_1_out30, decoder_1_out31;
  wire [4:0] \列选_t ;
  wire [31:0] multiplexer_1_out, register_32_q;

  Decoder #(.select(5), .tristate("false"), .disabled("Z"), .enable("false")) decoder_1 (
    .out0(decoder_1_out0), .out1(decoder_1_out1), .out2(decoder_1_out2), .out3(decoder_1_out3),
    .out4(decoder_1_out4), .out5(decoder_1_out5), .out6(decoder_1_out6), .out7(decoder_1_out7),
    .out8(decoder_1_out8), .out9(decoder_1_out9), .out10(decoder_1_out10), .out11(decoder_1_out11),
    .out12(decoder_1_out12), .out13(decoder_1_out13), .out14(decoder_1_out14), .out15(decoder_1_out15),
    .out16(decoder_1_out16), .out17(decoder_1_out17), .out18(decoder_1_out18), .out19(decoder_1_out19),
    .out20(decoder_1_out20), .out21(decoder_1_out21), .out22(decoder_1_out22), .out23(decoder_1_out23),
    .out24(decoder_1_out24), .out25(decoder_1_out25), .out26(decoder_1_out26), .out27(decoder_1_out27),
    .out28(decoder_1_out28), .out29(decoder_1_out29), .out30(decoder_1_out30), .out31(decoder_1_out31),
    .sel(\列选_t ));
  Multiplexer #(.select(1), .width(32), .disabled("Z"), .enable("false")) multiplexer_1 (
    .in0(\列数据 ), .in1({32{1'b0}}), .out(multiplexer_1_out), .sel(\同步清零_高电平有效 ));
  Register #(.width(32), .trigger("rising"), .Select("low")) register_1 (
    .D(multiplexer_1_out), .en(decoder_1_out0), .Q(_1), .clk(in_3), .clr(\清零_高电平有效 ));
  Register #(.width(32), .trigger("rising"), .Select("low")) register_2 (
    .D(multiplexer_1_out), .en(decoder_1_out1), .Q(out_8), .clk(in_3), .clr(\清零_高电平有效 ), .preset(\清零_高电平有效 ));  // open: cs
  Register #(.width(32), .trigger("rising"), .Select("low")) register_3 (
    .D(multiplexer_1_out), .en(decoder_1_out2), .Q(out_9), .clk(in_3), .clr(\清零_高电平有效 ), .preset(\清零_高电平有效 ));  // open: cs
  Register #(.width(32), .trigger("rising"), .Select("low")) register_4 (
    .D(multiplexer_1_out), .en(decoder_1_out3), .Q(out_10), .clk(in_3), .clr(\清零_高电平有效 ), .preset(\清零_高电平有效 ));  // open: cs
  Register #(.width(32), .trigger("rising"), .Select("low")) register_5 (
    .D(multiplexer_1_out), .en(decoder_1_out4), .Q(out_11), .clk(in_3), .clr(\清零_高电平有效 ), .preset(\清零_高电平有效 ));  // open: cs
  Register #(.width(32), .trigger("rising"), .Select("low")) register_6 (
    .D(multiplexer_1_out), .en(decoder_1_out5), .Q(out_12), .clk(in_3), .clr(\清零_高电平有效 ), .preset(\清零_高电平有效 ));  // open: cs
  Register #(.width(32), .trigger("rising"), .Select("low")) register_7 (
    .D(multiplexer_1_out), .en(decoder_1_out6), .Q(out_13), .clk(in_3), .clr(\清零_高电平有效 ), .preset(\清零_高电平有效 ));  // open: cs
  Register #(.width(32), .trigger("rising"), .Select("low")) register_8 (
    .D(multiplexer_1_out), .en(decoder_1_out7), .Q(out_14), .clk(in_3), .clr(\清零_高电平有效 ), .preset(\清零_高电平有效 ));  // open: cs
  Register #(.width(32), .trigger("rising"), .Select("low")) register_9 (
    .D(multiplexer_1_out), .en(decoder_1_out8), .Q(out_15), .clk(in_3), .clr(\清零_高电平有效 ));
  Register #(.width(32), .trigger("rising"), .Select("low")) register_10 (
    .D(multiplexer_1_out), .en(decoder_1_out9), .Q(out_16), .clk(in_3), .clr(\清零_高电平有效 ), .preset(\清零_高电平有效 ));  // open: cs
  Register #(.width(32), .trigger("rising"), .Select("low")) register_11 (
    .D(multiplexer_1_out), .en(decoder_1_out10), .Q(out_17), .clk(in_3), .clr(\清零_高电平有效 ), .preset(\清零_高电平有效 ));  // open: cs
  Register #(.width(32), .trigger("rising"), .Select("low")) register_12 (
    .D(multiplexer_1_out), .en(decoder_1_out11), .Q(out_18), .clk(in_3), .clr(\清零_高电平有效 ), .preset(\清零_高电平有效 ));  // open: cs
  Register #(.width(32), .trigger("rising"), .Select("low")) register_13 (
    .D(multiplexer_1_out), .en(decoder_1_out12), .Q(out_19), .clk(in_3), .clr(\清零_高电平有效 ), .preset(\清零_高电平有效 ));  // open: cs
  Register #(.width(32), .trigger("rising"), .Select("low")) register_14 (
    .D(multiplexer_1_out), .en(decoder_1_out13), .Q(out_20), .clk(in_3), .clr(\清零_高电平有效 ), .preset(\清零_高电平有效 ));  // open: cs
  Register #(.width(32), .trigger("rising"), .Select("low")) register_15 (
    .D(multiplexer_1_out), .en(decoder_1_out14), .Q(out_21), .clk(in_3), .clr(\清零_高电平有效 ), .preset(\清零_高电平有效 ));  // open: cs
  Register #(.width(32), .trigger("rising"), .Select("low")) register_16 (
    .D(multiplexer_1_out), .en(decoder_1_out15), .Q(out_22), .clk(in_3), .clr(\清零_高电平有效 ), .preset(\清零_高电平有效 ));  // open: cs
  Register #(.width(32), .trigger("rising"), .Select("low")) register_17 (
    .D(multiplexer_1_out), .en(decoder_1_out16), .Q(out_23), .clk(in_3), .clr(\清零_高电平有效 ));
  Register #(.width(32), .trigger("rising"), .Select("low")) register_18 (
    .D(multiplexer_1_out), .en(decoder_1_out17), .Q(out_24), .clk(in_3), .clr(\清零_高电平有效 ), .preset(\清零_高电平有效 ));  // open: cs
  Register #(.width(32), .trigger("rising"), .Select("low")) register_19 (
    .D(multiplexer_1_out), .en(decoder_1_out18), .Q(out_25), .clk(in_3), .clr(\清零_高电平有效 ), .preset(\清零_高电平有效 ));  // open: cs
  Register #(.width(32), .trigger("rising"), .Select("low")) register_20 (
    .D(multiplexer_1_out), .en(decoder_1_out19), .Q(out_26), .clk(in_3), .clr(\清零_高电平有效 ), .preset(\清零_高电平有效 ));  // open: cs
  Register #(.width(32), .trigger("rising"), .Select("low")) register_21 (
    .D(multiplexer_1_out), .en(decoder_1_out20), .Q(out_27), .clk(in_3), .clr(\清零_高电平有效 ), .preset(\清零_高电平有效 ));  // open: cs
  Register #(.width(32), .trigger("rising"), .Select("low")) register_22 (
    .D(multiplexer_1_out), .en(decoder_1_out21), .Q(out_28), .clk(in_3), .clr(\清零_高电平有效 ), .preset(\清零_高电平有效 ));  // open: cs
  Register #(.width(32), .trigger("rising"), .Select("low")) register_23 (
    .D(multiplexer_1_out), .en(decoder_1_out22), .Q(out_29), .clk(in_3), .clr(\清零_高电平有效 ), .preset(\清零_高电平有效 ));  // open: cs
  Register #(.width(32), .trigger("rising"), .Select("low")) register_24 (
    .D(multiplexer_1_out), .en(decoder_1_out23), .Q(out_30), .clk(in_3), .clr(\清零_高电平有效 ), .preset(\清零_高电平有效 ));  // open: cs
  Register #(.width(32), .trigger("rising"), .Select("low")) register_25 (
    .D(multiplexer_1_out), .en(decoder_1_out24), .Q(out_31), .clk(in_3), .clr(\清零_高电平有效 ));
  Register #(.width(32), .trigger("rising"), .Select("low")) register_26 (
    .D(multiplexer_1_out), .en(decoder_1_out25), .Q(out_32), .clk(in_3), .clr(\清零_高电平有效 ), .preset(\清零_高电平有效 ));  // open: cs
  Register #(.width(32), .trigger("rising"), .Select("low")) register_27 (
    .D(multiplexer_1_out), .en(decoder_1_out26), .Q(out_33), .clk(in_3), .clr(\清零_高电平有效 ), .preset(\清零_高电平有效 ));  // open: cs
  Register #(.width(32), .trigger("rising"), .Select("low")) register_28 (
    .D(multiplexer_1_out), .en(decoder_1_out27), .Q(out_34), .clk(in_3), .clr(\清零_高电平有效 ), .preset(\清零_高电平有效 ));  // open: cs
  Register #(.width(32), .trigger("rising"), .Select("low")) register_29 (
    .D(multiplexer_1_out), .en(decoder_1_out28), .Q(out_35), .clk(in_3), .clr(\清零_高电平有效 ), .preset(\清零_高电平有效 ));  // open: cs
  Register #(.width(32), .trigger("rising"), .Select("low")) register_30 (
    .D(multiplexer_1_out), .en(decoder_1_out29), .Q(out_36), .clk(in_3), .clr(\清零_高电平有效 ), .preset(\清零_高电平有效 ));  // open: cs
  Register #(.width(32), .trigger("rising"), .Select("low")) register_31 (
    .D(multiplexer_1_out), .en(decoder_1_out30), .Q(out_37), .clk(in_3), .clr(\清零_高电平有效 ), .preset(\清零_高电平有效 ));  // open: cs
  Register #(.width(32), .trigger("rising"), .Select("low")) register_32 (
    .D(multiplexer_1_out), .en(decoder_1_out31), .Q(register_32_q), .clk(in_3), .clr(\清零_高电平有效 ),
    .preset(\清零_高电平有效 ));  // open: cs
  or or_1 (\列选_t [4], \列选 [4], \使能_低电平有效 );
  or or_2 (\列选_t [3], \列选 [3], \使能_低电平有效 );
  or or_3 (\列选_t [2], \列选 [2], \使能_低电平有效 );
  or or_4 (\列选_t [1], \列选 [1], \使能_低电平有效 );
  or or_5 (\列选_t [0], \列选 [0], \使能_低电平有效 );

  // Other names for the same wires on the sheet: _2[31:0] = out_8; _3[31:0] = out_9; _4[31:0] = out_10;
  //   _5[31:0] = out_11; _6[31:0] = out_12; _7[31:0] = out_13; _8[31:0] = out_14; _9[31:0] = out_15;
  //   _10[31:0] = out_16; _11[31:0] = out_17; _12[31:0] = out_18; _13[31:0] = out_19; _14[31:0] = out_20;
  //   _15[31:0] = out_21; _16[31:0] = out_22; _17[31:0] = out_23; _18[31:0] = out_24; _19[31:0] = out_25;
  //   _20[31:0] = out_26; _21[31:0] = out_27; _22[31:0] = out_28; _23[31:0] = out_29; _24[31:0] = out_30;
  //   _25[31:0] = out_31; _26[31:0] = out_32; _27[31:0] = out_33; _28[31:0] = out_34; _29[31:0] = out_35;
  //   _30[31:0] = out_36; _31[31:0] = out_37
endmodule

module \手写数字识别  (
  input  IR1
);

  wire _011, _11, _012, _12, _013, _13, _014, _14, _015, _15, _016, _16, _017, _17, _018, _18, _021, _21,
       _022, _22, _023, _23, _024, _24, _025, _25, _026, _26, _027, _27, _028, _28, _031, _31, _032, _32,
       _033, _33, _034, _34, _035, _35, _036, _36, _037, _37, _038, _38, _041, _41, _042, _42, _043, _43,
       _044, _44, _045, _45, _046, _46, _047, _47, _048, _48, _051, _51, _052, _52, _053, _53, _054, _54,
       _055, _55, _056, _56, _057, _57, _058, _58, _061, _61, _062, _62, _063, _63, _064, _64, _065, _65,
       _066, _66, _067, _67, _068, _68, _071, _71, _072, _72, _073, _73, _074, _74, _075, _75, _076, _76,
       _077, _77, _078, _78, _081, _81, _082, _82, _083, _83, _084, _84, _085, _85, _086, _86, _087, _87,
       _088, _88, and_1_out, and_2_out, and_3_out, and_4_out, and_5_out, and_6_out, and_7_out, and_8_out,
       and_9_out, and_10_out, and_11_out, and_12_out, B, BEGZ, CLK, clr, d_ff_1_q, d_ff_2_q, d_ff_3_q,
       d_ff_4_qn, d_ff_5_qn, d_ff_6_qn, d_ff_7_qn, d_ff_8_qn, d_ff_9_qn, d_ff_10_qn, d_ff_11_qn, d_ff_12_qn,
       d_ff_13_qn, d_ff_14_qn, d_ff_15_qn, d_ff_16_qn, d_ff_17_qn, d_ff_18_qn, d_ff_19_qn, d_ff_20_qn,
       d_ff_21_qn, d_ff_22_qn, d_ff_23_qn, d_ff_24_qn, d_ff_25_qn, d_ff_26_qn, d_ff_27_qn, d_ff_28_qn,
       d_ff_29_qn, d_ff_30_qn, d_ff_31_qn, d_ff_32_qn, d_ff_33_qn, d_ff_34_qn, d_ff_35_qn, d_ff_36_qn,
       d_ff_37_qn, d_ff_38_qn, d_ff_39_qn, d_ff_40_qn, d_ff_41_qn, d_ff_42_qn, d_ff_43_qn, d_ff_44_qn,
       d_ff_45_qn, d_ff_46_qn, d_ff_47_qn, d_ff_48_qn, d_ff_49_qn, d_ff_50_qn, d_ff_51_qn, d_ff_52_qn,
       d_ff_53_qn, d_ff_54_qn, d_ff_55_qn, d_ff_56_qn, d_ff_57_qn, d_ff_58_qn, d_ff_59_qn, d_ff_60_qn,
       d_ff_61_qn, d_ff_62_qn, d_ff_63_qn, d_ff_64_qn, d_ff_65_qn, d_ff_66_qn, d_ff_67_qn, d_ff_68_qn,
       decoder_1_out0, decoder_1_out1, decoder_1_out2, decoder_1_out3, decoder_2_out1, decoder_2_out2,
       decoder_2_out3, ERET, Go, halt, IR1_2_q, IR1_3_q, IR1_q, IR1_t, IR2, IR3, IRA, J, JAL, Jr, MemWrite,
       MFC0, MTC0, not_1_out, not_2_out, not_3_out, not_4_out, not_5_out, not_6_out, or_9_out, or_10_out,
       or_11_out, or_12_out, or_13_out, or_15_out, RegDst, RegWrite, SB, SignedExt, W1, W2, W3, \中断开始 ,
       \单周期硬布线控制器_1_alu_src , \单周期硬布线控制器_1_beq , \单周期硬布线控制器_1_bne , \单周期硬布线控制器_1_memtoreg ,
       \单周期硬布线控制器_1_syscall ;
  wire [1:0] ByteSel, choice, RwChois, \中断选择 ;
  wire [3:0] \单周期硬布线控制器_1_alu_op ;
  wire [4:0] multiplexer_3_out, multiplexer_4_out, multiplexer_17_out, \地址0 , \地址1 ;
  wire [7:0] multiplexer_7_out, multiplexer_8_out, multiplexer_9_out, multiplexer_10_out;
  wire [15:0] \总周期数 ;
  wire [31:0] adder_1_out, adder_2_out, bit_extender_1_out, bit_extender_2_out, bit_extender_3_out, IR,
       LedData, MDin, MDout, multiplexer_1_out, multiplexer_2_out, multiplexer_6_out, multiplexer_11_out,
       multiplexer_12_out, multiplexer_14_out, multiplexer_16_out, multiplexer_18_out, multiplexer_20_out,
       PC, Rb, RDin, register_1_q, registerfile_1_p7, shifter_1_out, shifter_2_out;
  wire [31:2] mips_alu_1_result;

  Clock #(.highDuration(1), .lowDuration(1)) clock_1 (.out(CLK));
  or or_1 (IR1_t, IR1, IRA);
  Button _2 (.out(IR2));
  Button _3 (.out(IR3));
  not not_1 (not_1_out, Go);
  and and_1 (and_1_out, halt, not_1_out, \单周期硬布线控制器_1_syscall );
  not not_2 (not_2_out, and_1_out);
  LED #(.active("true")) led_1 (.in(W1));
  LED #(.active("true")) led_2 (.in(W2));
  LED #(.active("true")) led_3 (.in(W3));
  Counter #(.width(16), .max('hffff), .ongoal("wrap"), .trigger("rising"), .behavior("old")) \u_计数器  (
    .count(not_2_out), .Q(\总周期数 ), .clk(CLK), .clr(clr));  // open: load, D, carry, preset
  Hex_Digit_Display hex_digit_display_1 (.value(LedData[31:28]));  // open: dp
  Multiplexer #(.select(2), .width(32), .disabled("Z"), .enable("false")) multiplexer_1 (
    .in0(multiplexer_2_out), .in1(32'h8), .in2(32'h3150), .in3(32'h8), .out(multiplexer_1_out), .sel(\中断选择 ));
  Hex_Digit_Display hex_digit_display_2 (.value(LedData[27:24]));  // open: dp
  Hex_Digit_Display hex_digit_display_3 (.value(LedData[23:20]));  // open: dp
  Button button_1 (.out(clr));
  or or_2 (RwChois[1], JAL, BEGZ);
  or or_3 (RwChois[0], JAL, RegDst);
  Button \u_继续运行  (.out(Go));
  Register #(.width(32), .trigger("rising"), .Select("low")) u_PC (
    .D(multiplexer_1_out), .en(not_2_out), .Q(PC), .clk(CLK), .clr(clr));
  or or_4 (choice[1], Jr, JAL, J);
  or or_5 (choice[0], JAL, J, B);
  D_Flip_Flop #(.trigger("rising"), .Pre_Clr_Positions("LEGACY"), .NegatePresetClear("false"), .enable("true"), .NewFFLayout("false")) d_ff_1 (
    .clk(IR1_t), .D(1'b1), .Q(d_ff_1_q), .reset(IR1_q));  // open: Qn, preset, en
  or or_6 (W1, IR1_q, d_ff_1_q);
  D_Flip_Flop #(.trigger("rising"), .Pre_Clr_Positions("LEGACY"), .NegatePresetClear("false"), .enable("true"), .NewFFLayout("false")) d_ff_2 (
    .clk(IR2), .D(1'b1), .Q(d_ff_2_q), .reset(IR1_2_q));  // open: Qn, preset, en
  or or_7 (W2, IR1_2_q, d_ff_2_q);
  D_Flip_Flop #(.trigger("rising"), .Pre_Clr_Positions("LEGACY"), .NegatePresetClear("false"), .enable("true"), .NewFFLayout("false")) d_ff_3 (
    .clk(IR3), .D(1'b1), .Q(d_ff_3_q), .reset(IR1_3_q));  // open: Qn, preset, en
  or or_8 (W3, IR1_3_q, d_ff_3_q);
  Hex_Digit_Display hex_digit_display_4 (.value(LedData[19:16]));  // open: dp
  Hex_Digit_Display hex_digit_display_5 (.value(LedData[15:12]));  // open: dp
  Adder #(.width(32)) adder_1 (.a(PC), .b(32'h4), .out(adder_1_out));  // open: cin, cout
  Register #(.width(32), .trigger("rising"), .Select("low")) register_1 (
    .D(multiplexer_2_out), .en(\中断开始 ), .Q(register_1_q), .clk(CLK), .clr(clr));
  Multiplexer #(.select(1), .width(32), .disabled("Z"), .enable("false")) multiplexer_2 (
    .in0(multiplexer_14_out), .in1(register_1_q), .out(multiplexer_2_out), .sel(ERET));
  or or_9 (or_9_out, d_ff_1_q, IR1_q);
  or or_10 (or_10_out, d_ff_2_q, IR1_2_q);
  or or_11 (or_11_out, d_ff_3_q, IR1_3_q);
  Hex_Digit_Display hex_digit_display_6 (.value(LedData[11:8]));  // open: dp
  Hex_Digit_Display hex_digit_display_7 (.value(LedData[7:4]));  // open: dp
  // Probe on \总周期数 
  // Probe on register_1_q
  and and_2 (and_2_out, or_9_out, ~decoder_2_out1);  // AND_Gate
  and and_3 (and_3_out, or_10_out, ~decoder_2_out2);  // AND_Gate
  and and_4 (and_4_out, or_11_out, ~decoder_2_out3);  // AND_Gate
  Hex_Digit_Display hex_digit_display_8 (.value(LedData[3:0]));  // open: dp
  // Mips_Probe mips_probe_1: pin names not known; wires that end beside it: IR, IR[15:0]
  ROM #(.addrWidth(10), .dataWidth(32), .Select("high")) rom_1 (.addr(PC[11:2]), .data(IR));
  D_Flip_Flop #(.trigger("rising"), .Pre_Clr_Positions("LEGACY"), .NegatePresetClear("false"), .enable("true"), .NewFFLayout("false")) u_IR1 (
    .clk(CLK), .D(and_2_out), .Q(IR1_q), .reset(clr));  // open: Qn, preset, en
  D_Flip_Flop #(.trigger("rising"), .Pre_Clr_Positions("LEGACY"), .NegatePresetClear("false"), .enable("true"), .NewFFLayout("false")) IR1_2 (
    .clk(CLK), .D(and_3_out), .Q(IR1_2_q), .reset(clr));  // open: Qn, preset, en
  D_Flip_Flop #(.trigger("rising"), .Pre_Clr_Positions("LEGACY"), .NegatePresetClear("false"), .enable("true"), .NewFFLayout("false")) IR1_3 (
    .clk(CLK), .D(and_4_out), .Q(IR1_3_q), .reset(clr));  // open: Qn, preset, en
  Multiplexer #(.select(1), .width(5), .disabled("Z"), .enable("false")) multiplexer_3 (
    .in0(IR[20:16]), .in1(5'b00010), .out(multiplexer_3_out), .sel(\单周期硬布线控制器_1_syscall ));
  assign bit_extender_1_out = {{16{IR[15]}}, IR[15:0]};  // Bit_Extender bit_extender_1
  assign bit_extender_2_out = {{16{1'b0}}, IR[15:0]};  // Bit_Extender bit_extender_2
  assign bit_extender_3_out = {{6{1'b0}}, IR[25:0]};  // Bit_Extender bit_extender_3
  Decoder #(.select(2), .tristate("false"), .disabled("Z"), .enable("false")) decoder_1 (
    .out0(decoder_1_out0), .out1(decoder_1_out1), .out2(decoder_1_out2), .out3(decoder_1_out3), .sel(ByteSel));
  Button button_2 (.out(_21));
  Button button_3 (.out(_11));
  Button button_4 (.out(_22));
  Button button_5 (.out(_12));
  Button button_6 (.out(_13));
  Button button_7 (.out(_23));
  Button button_8 (.out(_14));
  Button button_9 (.out(_24));
  Button button_10 (.out(_15));
  Button button_11 (.out(_25));
  Button button_12 (.out(_26));
  Button button_13 (.out(_16));
  Button button_14 (.out(_17));
  Button button_15 (.out(_27));
  Button button_16 (.out(_28));
  Button button_17 (.out(_18));
  \单周期硬布线控制器  \u_单周期硬布线控制器_1  (
    .Func(IR[5:0]), .OP(IR[31:26]), .ALU_OP(\单周期硬布线控制器_1_alu_op ), .MemToReg(\单周期硬布线控制器_1_memtoreg ),
    .MemWrite(MemWrite), .ALU_SRC(\单周期硬布线控制器_1_alu_src ), .RegWrite(RegWrite),
    .SysCALL(\单周期硬布线控制器_1_syscall ), .SignedExt(SignedExt), .RegDst(RegDst), .JR(Jr), .JMP(J),
    .Beq(\单周期硬布线控制器_1_beq ), .JAL(JAL), .Bne(\单周期硬布线控制器_1_bne ), .SB(SB), .BEGZ(BEGZ), .T_F(IR[25:21]),
    .ERET(ERET), .MFC0(MFC0), .MTC0(MTC0));
  Multiplexer #(.select(1), .width(5), .disabled("Z"), .enable("false")) multiplexer_4 (
    .in0(IR[25:21]), .in1(5'b00100), .out(multiplexer_4_out), .sel(\单周期硬布线控制器_1_syscall ));
  Multiplexer #(.select(2), .width(5), .disabled("Z"), .enable("false")) multiplexer_5 (
    .in0(IR[20:16]), .in1(IR[15:11]), .in2({5{1'b0}}), .in3({5{1'b1}}), .out(\地址0 ), .sel(RwChois));
  and and_5 (and_5_out, IR1_q, d_ff_4_qn);
  and and_6 (and_6_out, IR1_2_q, d_ff_4_qn);
  and and_7 (and_7_out, IR1_3_q, d_ff_4_qn);
  or or_12 (or_12_out, decoder_2_out1, decoder_2_out2, decoder_2_out3);
  Button button_18 (.out(_41));
  Button button_19 (.out(_51));
  Button button_20 (.out(_31));
  Button button_21 (.out(_61));
  Button button_22 (.out(_32));
  Button button_23 (.out(_52));
  Button button_24 (.out(_42));
  Button button_25 (.out(_62));
  Button button_26 (.out(_53));
  Button button_27 (.out(_43));
  Button button_28 (.out(_33));
  Button button_29 (.out(_63));
  Button button_30 (.out(_44));
  Button button_31 (.out(_34));
  Button button_32 (.out(_54));
  Button button_33 (.out(_64));
  Button button_34 (.out(_35));
  Button button_35 (.out(_65));
  Button button_36 (.out(_45));
  Button button_37 (.out(_55));
  Button button_38 (.out(_56));
  Button button_39 (.out(_46));
  Button button_40 (.out(_66));
  Button button_41 (.out(_36));
  Button button_42 (.out(_57));
  Button button_43 (.out(_67));
  Button button_44 (.out(_47));
  Button button_45 (.out(_37));
  Button button_46 (.out(_68));
  Button button_47 (.out(_38));
  Button button_48 (.out(_58));
  Button button_49 (.out(_48));
  or or_13 (or_13_out, MFC0, RegWrite, MTC0);
  Multiplexer #(.select(1), .width(32), .disabled("Z"), .enable("false")) multiplexer_6 (
    .in0(bit_extender_2_out), .in1(bit_extender_1_out), .out(multiplexer_6_out), .sel(SignedExt));
  or or_14 (\中断选择 [1], and_7_out, and_6_out);
  not not_3 (not_3_out, and_6_out);
  or or_15 (or_15_out, or_12_out, ERET);
  Button button_50 (.out(_81));
  Button button_51 (.out(_71));
  Button button_52 (.out(_82));
  Button button_53 (.out(_72));
  Button button_54 (.out(_73));
  Button button_55 (.out(_83));
  Button button_56 (.out(_84));
  Button button_57 (.out(_74));
  Button button_58 (.out(_75));
  Button button_59 (.out(_85));
  Button button_60 (.out(_76));
  Button button_61 (.out(_86));
  DotMatrix #(.inputtype("column"), .matrixcols(8), .matrixrows(8), .persist(0), .dotshape("square")) dotmatrix_1 (
    .col0({_011, _012, _013, _014, _015, _016, _017, _018}),
    .col1({_021, _022, _023, _024, _025, _026, _027, _028}),
    .col2({_031, _032, _033, _034, _035, _036, _037, _038}),
    .col3({_041, _042, _043, _044, _045, _046, _047, _048}),
    .col4({_051, _052, _053, _054, _055, _056, _057, _058}),
    .col5({_061, _062, _063, _064, _065, _066, _067, _068}),
    .col6({_071, _072, _073, _074, _075, _076, _077, _078}),
    .col7({_081, _082, _083, _084, _085, _086, _087, _088}));
  Button button_62 (.out(_87));
  Button button_63 (.out(_77));
  Button button_64 (.out(_88));
  Button button_65 (.out(_78));
  Multiplexer #(.select(1), .width(8), .disabled("Z"), .enable("false")) multiplexer_7 (
    .in0(MDout[7:0]), .in1(Rb[7:0]), .out(multiplexer_7_out), .sel(decoder_1_out0));
  Multiplexer #(.select(1), .width(8), .disabled("Z"), .enable("false")) multiplexer_8 (
    .in0(MDout[15:8]), .in1(Rb[7:0]), .out(multiplexer_8_out), .sel(decoder_1_out1));
  Multiplexer #(.select(1), .width(8), .disabled("Z"), .enable("false")) multiplexer_9 (
    .in0(MDout[23:16]), .in1(Rb[7:0]), .out(multiplexer_9_out), .sel(decoder_1_out2));
  Multiplexer #(.select(1), .width(8), .disabled("Z"), .enable("false")) multiplexer_10 (
    .in0(MDout[31:24]), .out(multiplexer_10_out), .sel(decoder_1_out3));  // open: in1
  and and_8 (and_8_out, and_5_out, not_3_out);
  D_Flip_Flop #(.trigger("rising"), .Pre_Clr_Positions("LEGACY"), .NegatePresetClear("false"), .enable("true"), .NewFFLayout("false")) d_ff_4 (
    .clk(CLK), .D(or_12_out), .Qn(d_ff_4_qn), .en(or_15_out), .reset(clr));  // open: Q, preset
  // RegisterFile registerfile_1: pin names not known; wires that end beside it: RDin, CLK, or_13_out, \地址1 , multiplexer_4_out, multiplexer_3_out, registerfile_1_p7, Rb
  Shifter #(.width(32), .shift("ll")) shifter_1 (.in(bit_extender_1_out), .\dist (5'b00010), .out(shifter_1_out));
  Shifter #(.width(32), .shift("ll")) shifter_2 (.in(bit_extender_3_out), .\dist (5'b00010), .out(shifter_2_out));
  or or_16 (\中断开始 , and_5_out, and_6_out, and_7_out);
  or or_17 (\中断选择 [0], and_7_out, and_8_out);
  Decoder #(.select(2), .tristate("false"), .disabled("Z"), .enable("false")) decoder_2 (
    .out1(decoder_2_out1), .out2(decoder_2_out2), .out3(decoder_2_out3), .sel(\中断选择 ));  // open: out0
  Button \u_开始预测  (.out(IRA));
  Multiplexer #(.select(1), .width(32), .disabled("Z"), .enable("false")) multiplexer_11 (
    .in0(registerfile_1_p7), .in1(32'h32), .out(multiplexer_11_out), .sel(\单周期硬布线控制器_1_syscall ));
  Multiplexer #(.select(1), .width(32), .disabled("Z"), .enable("false")) multiplexer_12 (
    .in0(Rb), .in1(multiplexer_6_out), .out(multiplexer_12_out), .sel(\单周期硬布线控制器_1_alu_src ));
  MIPS_ALU mips_alu_1 (
    .X(multiplexer_11_out), .Y(multiplexer_12_out), .AluOP(\单周期硬布线控制器_1_alu_op ), .Equal(halt),
    .Result({mips_alu_1_result, ByteSel}), .shamt(IR[10:6]));  // open: Result_2
  Adder #(.width(32)) adder_2 (.a(adder_1_out), .b(shifter_1_out), .out(adder_2_out));  // open: cin, cout
  Multiplexer #(.select(1), .width(32), .disabled("Z"), .enable("false")) multiplexer_13 (
    .in0(Rb), .in1({multiplexer_10_out, multiplexer_9_out, multiplexer_8_out, multiplexer_7_out}),
    .out(MDin), .sel(SB));
  and and_9 (and_9_out, BEGZ, not_4_out);
  not not_4 (not_4_out, ByteSel[0]);
  and and_10 (and_10_out, \单周期硬布线控制器_1_beq , halt);
  and and_11 (and_11_out, \单周期硬布线控制器_1_bne , not_5_out);
  not not_5 (not_5_out, halt);
  not not_6 (not_6_out, halt);
  and and_12 (and_12_out, not_6_out, \单周期硬布线控制器_1_syscall );
  Multiplexer #(.select(2), .width(32), .disabled("Z"), .enable("false")) multiplexer_14 (
    .in0(adder_1_out), .in1(adder_2_out), .in2(registerfile_1_p7), .in3(shifter_2_out),
    .out(multiplexer_14_out), .sel(choice));
  or or_18 (B, and_9_out, and_10_out, and_11_out);
  Register #(.width(32), .trigger("rising"), .Select("low")) \u_显示锁存  (
    .D(registerfile_1_p7), .en(and_12_out), .Q(LedData), .clk(CLK), .clr(clr));
  RAM #(.addrWidth(10), .dataWidth(32), .bus("separate"), .Select("high")) ram_1 (
    .addr(mips_alu_1_result[11:2]), .din(MDin), .data(MDout), .str(MemWrite), .clk(CLK), .clr(clr));  // open: sel, ld
  Multiplexer #(.select(1), .width(32), .disabled("Z"), .enable("false")) multiplexer_15 (
    .in0(multiplexer_20_out), .in1(adder_1_out), .out(RDin), .sel(JAL));
  Multiplexer #(.select(1), .width(32), .disabled("Z"), .enable("false")) multiplexer_16 (
    .in0({mips_alu_1_result, ByteSel}), .in1(MDout), .out(multiplexer_16_out), .sel(\单周期硬布线控制器_1_memtoreg ));
  Multiplexer #(.select(1), .width(5), .disabled("Z"), .enable("false")) multiplexer_17 (
    .in0(\地址0 ), .in1(5'b00001), .out(multiplexer_17_out), .sel(MFC0));
  Multiplexer #(.select(1), .width(32), .disabled("Z"), .enable("false")) multiplexer_18 (
    .in0(multiplexer_16_out),
    .in1({_011, _021, _031, _041, _051, _061, _071, _081, _012, _022, _032, _042, _052, _062, _072, _082, _013, _023, _033, _043, _053, _063, _073, _083, _014, _024, _034, _044, _054, _064, _074, _084}),
    .out(multiplexer_18_out), .sel(MFC0));
  Multiplexer #(.select(1), .width(5), .disabled("Z"), .enable("false")) multiplexer_19 (
    .in0(multiplexer_17_out), .in1(5'b00010), .out(\地址1 ), .sel(MTC0));
  Multiplexer #(.select(1), .width(32), .disabled("Z"), .enable("false")) multiplexer_20 (
    .in0(multiplexer_18_out),
    .in1({_015, _025, _035, _045, _055, _065, _075, _085, _016, _026, _036, _046, _056, _066, _076, _086, _017, _027, _037, _047, _057, _067, _077, _087, _018, _028, _038, _048, _058, _068, _078, _088}),
    .out(multiplexer_20_out), .sel(MTC0));
  D_Flip_Flop #(.trigger("rising"), .Pre_Clr_Positions("LEGACY"), .NegatePresetClear("false"), .enable("true"), .NewFFLayout("false")) d_ff_5 (
    .clk(_11), .D(d_ff_5_qn), .Q(_011), .Qn(d_ff_5_qn));  // open: preset, en, reset
  D_Flip_Flop #(.trigger("rising"), .Pre_Clr_Positions("LEGACY"), .NegatePresetClear("false"), .enable("true"), .NewFFLayout("false")) d_ff_6 (
    .clk(_12), .D(d_ff_6_qn), .Q(_012), .Qn(d_ff_6_qn));  // open: preset, en, reset
  D_Flip_Flop #(.trigger("rising"), .Pre_Clr_Positions("LEGACY"), .NegatePresetClear("false"), .enable("true"), .NewFFLayout("false")) d_ff_7 (
    .clk(_13), .D(d_ff_7_qn), .Q(_013), .Qn(d_ff_7_qn));  // open: preset, en, reset
  D_Flip_Flop #(.trigger("rising"), .Pre_Clr_Positions("LEGACY"), .NegatePresetClear("false"), .enable("true"), .NewFFLayout("false")) d_ff_8 (
    .clk(_14), .D(d_ff_8_qn), .Q(_014), .Qn(d_ff_8_qn));  // open: preset, en, reset
  D_Flip_Flop #(.trigger("rising"), .Pre_Clr_Positions("LEGACY"), .NegatePresetClear("false"), .enable("true"), .NewFFLayout("false")) d_ff_9 (
    .clk(_15), .D(d_ff_9_qn), .Q(_015), .Qn(d_ff_9_qn));  // open: preset, en, reset
  D_Flip_Flop #(.trigger("rising"), .Pre_Clr_Positions("LEGACY"), .NegatePresetClear("false"), .enable("true"), .NewFFLayout("false")) d_ff_10 (
    .clk(_16), .D(d_ff_10_qn), .Q(_016), .Qn(d_ff_10_qn));  // open: preset, en, reset
  D_Flip_Flop #(.trigger("rising"), .Pre_Clr_Positions("LEGACY"), .NegatePresetClear("false"), .enable("true"), .NewFFLayout("false")) d_ff_11 (
    .clk(_17), .D(d_ff_11_qn), .Q(_017), .Qn(d_ff_11_qn));  // open: preset, en, reset
  D_Flip_Flop #(.trigger("rising"), .Pre_Clr_Positions("LEGACY"), .NegatePresetClear("false"), .enable("true"), .NewFFLayout("false")) d_ff_12 (
    .clk(_18), .D(d_ff_12_qn), .Q(_018), .Qn(d_ff_12_qn));  // open: preset, en, reset
  D_Flip_Flop #(.trigger("rising"), .Pre_Clr_Positions("LEGACY"), .NegatePresetClear("false"), .enable("true"), .NewFFLayout("false")) d_ff_13 (
    .clk(_21), .D(d_ff_13_qn), .Q(_021), .Qn(d_ff_13_qn));  // open: preset, en, reset
  D_Flip_Flop #(.trigger("rising"), .Pre_Clr_Positions("LEGACY"), .NegatePresetClear("false"), .enable("true"), .NewFFLayout("false")) d_ff_14 (
    .clk(_22), .D(d_ff_14_qn), .Q(_022), .Qn(d_ff_14_qn));  // open: preset, en, reset
  D_Flip_Flop #(.trigger("rising"), .Pre_Clr_Positions("LEGACY"), .NegatePresetClear("false"), .enable("true"), .NewFFLayout("false")) d_ff_15 (
    .clk(_23), .D(d_ff_15_qn), .Q(_023), .Qn(d_ff_15_qn));  // open: preset, en, reset
  D_Flip_Flop #(.trigger("rising"), .Pre_Clr_Positions("LEGACY"), .NegatePresetClear("false"), .enable("true"), .NewFFLayout("false")) d_ff_16 (
    .clk(_24), .D(d_ff_16_qn), .Q(_024), .Qn(d_ff_16_qn));  // open: preset, en, reset
  D_Flip_Flop #(.trigger("rising"), .Pre_Clr_Positions("LEGACY"), .NegatePresetClear("false"), .enable("true"), .NewFFLayout("false")) d_ff_17 (
    .clk(_25), .D(d_ff_17_qn), .Q(_025), .Qn(d_ff_17_qn));  // open: preset, en, reset
  D_Flip_Flop #(.trigger("rising"), .Pre_Clr_Positions("LEGACY"), .NegatePresetClear("false"), .enable("true"), .NewFFLayout("false")) d_ff_18 (
    .clk(_26), .D(d_ff_18_qn), .Q(_026), .Qn(d_ff_18_qn));  // open: preset, en, reset
  D_Flip_Flop #(.trigger("rising"), .Pre_Clr_Positions("LEGACY"), .NegatePresetClear("false"), .enable("true"), .NewFFLayout("false")) d_ff_19 (
    .clk(_27), .D(d_ff_19_qn), .Q(_027), .Qn(d_ff_19_qn));  // open: preset, en, reset
  D_Flip_Flop #(.trigger("rising"), .Pre_Clr_Positions("LEGACY"), .NegatePresetClear("false"), .enable("true"), .NewFFLayout("false")) d_ff_20 (
    .clk(_28), .D(d_ff_20_qn), .Q(_028), .Qn(d_ff_20_qn));  // open: preset, en, reset
  D_Flip_Flop #(.trigger("rising"), .Pre_Clr_Positions("LEGACY"), .NegatePresetClear("false"), .enable("true"), .NewFFLayout("false")) d_ff_21 (
    .clk(_31), .D(d_ff_21_qn), .Q(_031), .Qn(d_ff_21_qn));  // open: preset, en, reset
  D_Flip_Flop #(.trigger("rising"), .Pre_Clr_Positions("LEGACY"), .NegatePresetClear("false"), .enable("true"), .NewFFLayout("false")) d_ff_22 (
    .clk(_32), .D(d_ff_22_qn), .Q(_032), .Qn(d_ff_22_qn));  // open: preset, en, reset
  D_Flip_Flop #(.trigger("rising"), .Pre_Clr_Positions("LEGACY"), .NegatePresetClear("false"), .enable("true"), .NewFFLayout("false")) d_ff_23 (
    .clk(_33), .D(d_ff_23_qn), .Q(_033), .Qn(d_ff_23_qn));  // open: preset, en, reset
  D_Flip_Flop #(.trigger("rising"), .Pre_Clr_Positions("LEGACY"), .NegatePresetClear("false"), .enable("true"), .NewFFLayout("false")) d_ff_24 (
    .clk(_34), .D(d_ff_24_qn), .Q(_034), .Qn(d_ff_24_qn));  // open: preset, en, reset
  D_Flip_Flop #(.trigger("rising"), .Pre_Clr_Positions("LEGACY"), .NegatePresetClear("false"), .enable("true"), .NewFFLayout("false")) d_ff_25 (
    .clk(_35), .D(d_ff_25_qn), .Q(_035), .Qn(d_ff_25_qn));  // open: preset, en, reset
  D_Flip_Flop #(.trigger("rising"), .Pre_Clr_Positions("LEGACY"), .NegatePresetClear("false"), .enable("true"), .NewFFLayout("false")) d_ff_26 (
    .clk(_36), .D(d_ff_26_qn), .Q(_036), .Qn(d_ff_26_qn));  // open: preset, en, reset
  D_Flip_Flop #(.trigger("rising"), .Pre_Clr_Positions("LEGACY"), .NegatePresetClear("false"), .enable("true"), .NewFFLayout("false")) d_ff_27 (
    .clk(_37), .D(d_ff_27_qn), .Q(_037), .Qn(d_ff_27_qn));  // open: preset, en, reset
  D_Flip_Flop #(.trigger("rising"), .Pre_Clr_Positions("LEGACY"), .NegatePresetClear("false"), .enable("true"), .NewFFLayout("false")) d_ff_28 (
    .clk(_38), .D(d_ff_28_qn), .Q(_038), .Qn(d_ff_28_qn));  // open: preset, en, reset
  D_Flip_Flop #(.trigger("rising"), .Pre_Clr_Positions("LEGACY"), .NegatePresetClear("false"), .enable("true"), .NewFFLayout("false")) d_ff_29 (
    .clk(_41), .D(d_ff_29_qn), .Q(_041), .Qn(d_ff_29_qn));  // open: preset, en, reset
  D_Flip_Flop #(.trigger("rising"), .Pre_Clr_Positions("LEGACY"), .NegatePresetClear("false"), .enable("true"), .NewFFLayout("false")) d_ff_30 (
    .clk(_42), .D(d_ff_30_qn), .Q(_042), .Qn(d_ff_30_qn));  // open: preset, en, reset
  D_Flip_Flop #(.trigger("rising"), .Pre_Clr_Positions("LEGACY"), .NegatePresetClear("false"), .enable("true"), .NewFFLayout("false")) d_ff_31 (
    .clk(_43), .D(d_ff_31_qn), .Q(_043), .Qn(d_ff_31_qn));  // open: preset, en, reset
  D_Flip_Flop #(.trigger("rising"), .Pre_Clr_Positions("LEGACY"), .NegatePresetClear("false"), .enable("true"), .NewFFLayout("false")) d_ff_32 (
    .clk(_44), .D(d_ff_32_qn), .Q(_044), .Qn(d_ff_32_qn));  // open: preset, en, reset
  D_Flip_Flop #(.trigger("rising"), .Pre_Clr_Positions("LEGACY"), .NegatePresetClear("false"), .enable("true"), .NewFFLayout("false")) d_ff_33 (
    .clk(_45), .D(d_ff_33_qn), .Q(_045), .Qn(d_ff_33_qn));  // open: preset, en, reset
  D_Flip_Flop #(.trigger("rising"), .Pre_Clr_Positions("LEGACY"), .NegatePresetClear("false"), .enable("true"), .NewFFLayout("false")) d_ff_34 (
    .clk(_46), .D(d_ff_34_qn), .Q(_046), .Qn(d_ff_34_qn));  // open: preset, en, reset
  D_Flip_Flop #(.trigger("rising"), .Pre_Clr_Positions("LEGACY"), .NegatePresetClear("false"), .enable("true"), .NewFFLayout("false")) d_ff_35 (
    .clk(_47), .D(d_ff_35_qn), .Q(_047), .Qn(d_ff_35_qn));  // open: preset, en, reset
  D_Flip_Flop #(.trigger("rising"), .Pre_Clr_Positions("LEGACY"), .NegatePresetClear("false"), .enable("true"), .NewFFLayout("false")) d_ff_36 (
    .clk(_48), .D(d_ff_36_qn), .Q(_048), .Qn(d_ff_36_qn));  // open: preset, en, reset
  D_Flip_Flop #(.trigger("rising"), .Pre_Clr_Positions("LEGACY"), .NegatePresetClear("false"), .enable("true"), .NewFFLayout("false")) d_ff_37 (
    .clk(_51), .D(d_ff_37_qn), .Q(_051), .Qn(d_ff_37_qn));  // open: preset, en, reset
  D_Flip_Flop #(.trigger("rising"), .Pre_Clr_Positions("LEGACY"), .NegatePresetClear("false"), .enable("true"), .NewFFLayout("false")) d_ff_38 (
    .clk(_52), .D(d_ff_38_qn), .Q(_052), .Qn(d_ff_38_qn));  // open: preset, en, reset
  D_Flip_Flop #(.trigger("rising"), .Pre_Clr_Positions("LEGACY"), .NegatePresetClear("false"), .enable("true"), .NewFFLayout("false")) d_ff_39 (
    .clk(_53), .D(d_ff_39_qn), .Q(_053), .Qn(d_ff_39_qn));  // open: preset, en, reset
  D_Flip_Flop #(.trigger("rising"), .Pre_Clr_Positions("LEGACY"), .NegatePresetClear("false"), .enable("true"), .NewFFLayout("false")) d_ff_40 (
    .clk(_54), .D(d_ff_40_qn), .Q(_054), .Qn(d_ff_40_qn));  // open: preset, en, reset
  D_Flip_Flop #(.trigger("rising"), .Pre_Clr_Positions("LEGACY"), .NegatePresetClear("false"), .enable("true"), .NewFFLayout("false")) d_ff_41 (
    .clk(_55), .D(d_ff_41_qn), .Q(_055), .Qn(d_ff_41_qn));  // open: preset, en, reset
  D_Flip_Flop #(.trigger("rising"), .Pre_Clr_Positions("LEGACY"), .NegatePresetClear("false"), .enable("true"), .NewFFLayout("false")) d_ff_42 (
    .clk(_56), .D(d_ff_42_qn), .Q(_056), .Qn(d_ff_42_qn));  // open: preset, en, reset
  D_Flip_Flop #(.trigger("rising"), .Pre_Clr_Positions("LEGACY"), .NegatePresetClear("false"), .enable("true"), .NewFFLayout("false")) d_ff_43 (
    .clk(_57), .D(d_ff_43_qn), .Q(_057), .Qn(d_ff_43_qn));  // open: preset, en, reset
  D_Flip_Flop #(.trigger("rising"), .Pre_Clr_Positions("LEGACY"), .NegatePresetClear("false"), .enable("true"), .NewFFLayout("false")) d_ff_44 (
    .clk(_58), .D(d_ff_44_qn), .Q(_058), .Qn(d_ff_44_qn));  // open: preset, en, reset
  D_Flip_Flop #(.trigger("rising"), .Pre_Clr_Positions("LEGACY"), .NegatePresetClear("false"), .enable("true"), .NewFFLayout("false")) d_ff_45 (
    .clk(_61), .D(d_ff_45_qn), .Q(_061), .Qn(d_ff_45_qn));  // open: preset, en, reset
  D_Flip_Flop #(.trigger("rising"), .Pre_Clr_Positions("LEGACY"), .NegatePresetClear("false"), .enable("true"), .NewFFLayout("false")) d_ff_46 (
    .clk(_62), .D(d_ff_46_qn), .Q(_062), .Qn(d_ff_46_qn));  // open: preset, en, reset
  D_Flip_Flop #(.trigger("rising"), .Pre_Clr_Positions("LEGACY"), .NegatePresetClear("false"), .enable("true"), .NewFFLayout("false")) d_ff_47 (
    .clk(_63), .D(d_ff_47_qn), .Q(_063), .Qn(d_ff_47_qn));  // open: preset, en, reset
  D_Flip_Flop #(.trigger("rising"), .Pre_Clr_Positions("LEGACY"), .NegatePresetClear("false"), .enable("true"), .NewFFLayout("false")) d_ff_48 (
    .clk(_64), .D(d_ff_48_qn), .Q(_064), .Qn(d_ff_48_qn));  // open: preset, en, reset
  D_Flip_Flop #(.trigger("rising"), .Pre_Clr_Positions("LEGACY"), .NegatePresetClear("false"), .enable("true"), .NewFFLayout("false")) d_ff_49 (
    .clk(_65), .D(d_ff_49_qn), .Q(_065), .Qn(d_ff_49_qn));  // open: preset, en, reset
  D_Flip_Flop #(.trigger("rising"), .Pre_Clr_Positions("LEGACY"), .NegatePresetClear("false"), .enable("true"), .NewFFLayout("false")) d_ff_50 (
    .clk(_66), .D(d_ff_50_qn), .Q(_066), .Qn(d_ff_50_qn));  // open: preset, en, reset
  D_Flip_Flop #(.trigger("rising"), .Pre_Clr_Positions("LEGACY"), .NegatePresetClear("false"), .enable("true"), .NewFFLayout("false")) d_ff_51 (
    .clk(_67), .D(d_ff_51_qn), .Q(_067), .Qn(d_ff_51_qn));  // open: preset, en, reset
  D_Flip_Flop #(.trigger("rising"), .Pre_Clr_Positions("LEGACY"), .NegatePresetClear("false"), .enable("true"), .NewFFLayout("false")) d_ff_52 (
    .clk(_68), .D(d_ff_52_qn), .Q(_068), .Qn(d_ff_52_qn));  // open: preset, en, reset
  D_Flip_Flop #(.trigger("rising"), .Pre_Clr_Positions("LEGACY"), .NegatePresetClear("false"), .enable("true"), .NewFFLayout("false")) d_ff_53 (
    .clk(_71), .D(d_ff_53_qn), .Q(_071), .Qn(d_ff_53_qn));  // open: preset, en, reset
  D_Flip_Flop #(.trigger("rising"), .Pre_Clr_Positions("LEGACY"), .NegatePresetClear("false"), .enable("true"), .NewFFLayout("false")) d_ff_54 (
    .clk(_72), .D(d_ff_54_qn), .Q(_072), .Qn(d_ff_54_qn));  // open: preset, en, reset
  D_Flip_Flop #(.trigger("rising"), .Pre_Clr_Positions("LEGACY"), .NegatePresetClear("false"), .enable("true"), .NewFFLayout("false")) d_ff_55 (
    .clk(_73), .D(d_ff_55_qn), .Q(_073), .Qn(d_ff_55_qn));  // open: preset, en, reset
  D_Flip_Flop #(.trigger("rising"), .Pre_Clr_Positions("LEGACY"), .NegatePresetClear("false"), .enable("true"), .NewFFLayout("false")) d_ff_56 (
    .clk(_74), .D(d_ff_56_qn), .Q(_074), .Qn(d_ff_56_qn));  // open: preset, en, reset
  D_Flip_Flop #(.trigger("rising"), .Pre_Clr_Positions("LEGACY"), .NegatePresetClear("false"), .enable("true"), .NewFFLayout("false")) d_ff_57 (
    .clk(_75), .D(d_ff_57_qn), .Q(_075), .Qn(d_ff_57_qn));  // open: preset, en, reset
  D_Flip_Flop #(.trigger("rising"), .Pre_Clr_Positions("LEGACY"), .NegatePresetClear("false"), .enable("true"), .NewFFLayout("false")) d_ff_58 (
    .clk(_76), .D(d_ff_58_qn), .Q(_076), .Qn(d_ff_58_qn));  // open: preset, en, reset
  D_Flip_Flop #(.trigger("rising"), .Pre_Clr_Positions("LEGACY"), .NegatePresetClear("false"), .enable("true"), .NewFFLayout("false")) d_ff_59 (
    .clk(_77), .D(d_ff_59_qn), .Q(_077), .Qn(d_ff_59_qn));  // open: preset, en, reset
  D_Flip_Flop #(.trigger("rising"), .Pre_Clr_Positions("LEGACY"), .NegatePresetClear("false"), .enable("true"), .NewFFLayout("false")) d_ff_60 (
    .clk(_78), .D(d_ff_60_qn), .Q(_078), .Qn(d_ff_60_qn));  // open: preset, en, reset
  D_Flip_Flop #(.trigger("rising"), .Pre_Clr_Positions("LEGACY"), .NegatePresetClear("false"), .enable("true"), .NewFFLayout("false")) d_ff_61 (
    .clk(_81), .D(d_ff_61_qn), .Q(_081), .Qn(d_ff_61_qn));  // open: preset, en, reset
  D_Flip_Flop #(.trigger("rising"), .Pre_Clr_Positions("LEGACY"), .NegatePresetClear("false"), .enable("true"), .NewFFLayout("false")) d_ff_62 (
    .clk(_82), .D(d_ff_62_qn), .Q(_082), .Qn(d_ff_62_qn));  // open: preset, en, reset
  D_Flip_Flop #(.trigger("rising"), .Pre_Clr_Positions("LEGACY"), .NegatePresetClear("false"), .enable("true"), .NewFFLayout("false")) d_ff_63 (
    .clk(_83), .D(d_ff_63_qn), .Q(_083), .Qn(d_ff_63_qn));  // open: preset, en, reset
  D_Flip_Flop #(.trigger("rising"), .Pre_Clr_Positions("LEGACY"), .NegatePresetClear("false"), .enable("true"), .NewFFLayout("false")) d_ff_64 (
    .clk(_84), .D(d_ff_64_qn), .Q(_084), .Qn(d_ff_64_qn));  // open: preset, en, reset
  D_Flip_Flop #(.trigger("rising"), .Pre_Clr_Positions("LEGACY"), .NegatePresetClear("false"), .enable("true"), .NewFFLayout("false")) d_ff_65 (
    .clk(_85), .D(d_ff_65_qn), .Q(_085), .Qn(d_ff_65_qn));  // open: preset, en, reset
  D_Flip_Flop #(.trigger("rising"), .Pre_Clr_Positions("LEGACY"), .NegatePresetClear("false"), .enable("true"), .NewFFLayout("false")) d_ff_66 (
    .clk(_86), .D(d_ff_66_qn), .Q(_086), .Qn(d_ff_66_qn));  // open: preset, en, reset
  D_Flip_Flop #(.trigger("rising"), .Pre_Clr_Positions("LEGACY"), .NegatePresetClear("false"), .enable("true"), .NewFFLayout("false")) d_ff_67 (
    .clk(_87), .D(d_ff_67_qn), .Q(_087), .Qn(d_ff_67_qn));  // open: preset, en, reset
  D_Flip_Flop #(.trigger("rising"), .Pre_Clr_Positions("LEGACY"), .NegatePresetClear("false"), .enable("true"), .NewFFLayout("false")) d_ff_68 (
    .clk(_88), .D(d_ff_68_qn), .Q(_088), .Qn(d_ff_68_qn));  // open: preset, en, reset

  // Other names for the same wires on the sheet: result1_1 = ByteSel[0]; IRB = IR2; IRC = IR3;
  //   上半部分[31:0] = {_011, _021, _031, _041, _051, _061, _071, _081, _012, _022, _032, _042, _052, _062, _072, _082, _013, _023, _033, _043, _053, _063, _073, _083, _014, _024, _034, _044, _054, _064, _074, _084};
  //   下半部分[31:0] = {_015, _025, _035, _045, _055, _065, _075, _085, _016, _026, _036, _046, _056, _066, _076, _086, _017, _027, _037, _047, _057, _067, _077, _087, _018, _028, _038, _048, _058, _068, _078, _088}

  // Notes on the sheet:
  //   请在ROM中加载 pred.hex ,在RAM中加载 data.hex
  //   按Ctrl+K开始运行程序
  //   在按钮阵中输入手写数字后，点击开始预测按钮
  //   程序从点击预测到得出结果大约需要7000个时钟周期
  //   总复位信号应将除ROM以外所有存储组件全部清零
  //   数码管输出
  //   指令存储器
  //   PC选择信号
  //   指令字
  //   contents of rom_1 (hex, n*v repeats v):
  //   0 8100000 40021000 40821000 ac010be0 ac020be4 20050000 20060080 20090cfc 302a0001 a5100 10842
  //   1254022 ad0a0000 20a50004 14a6fff9 20050000 20060080 20090d7c 304a0001 a5100 21042 1254022 ad0a0000
  //   20a50004 14a6fff9 20040000 200e0c30 200f0a00 20050028 20060000 20080000 200c0c80 20070a00 865820
  //   8d690000 8d8a0000 218c0004 712a6802 10d4020 20c60028 14c7fff8 8df00000 1104020 8882a 71114002
  //   adc80000 21ef0004 21ce0004 20840004 1485ffeb 20040000 200e0c58 200f0bb8 20050028 20060000 20080000
  //   200c0c30 20070190 865820 8d690a28 8d8a0000 218c0004 712a6802 10d4020 20c60028 14c7fff8 8df00000
  //   1104020 adc80000 21ef0004 21ce0004 20840004 1485ffed 20040000 20050028 8c880c58 20090000 20840004
  //   20060001 8c8a0c58 10a582a 11600002 21480000 20c90000 20c60001 20840004 1485fff8 21240000 c 42000018
  //   8100000
  //   Reset 
  //   Reset 
  //   Reset 
  //   SB
  //   JMP
  //   JR
  //   OP
  //   Func
  //   T/F
  //   OP
  //   Func
  //   rs
  //   rt
  //   rd
  //   Beq
  //   Bne
  //   MemToReg
  //   MemWrite
  //   AluOP
  //   AluSrcB
  //   RegWrite
  //   JAL
  //   RegDst
  //   Syscall
  //   SB命令
  //   中断仲裁
endmodule
